// Logisim project Etch-a-Sketch.circ as structural Verilog
module main (
);

  wire cmd, counter_1_led, counter_2_led, drw, Er, L, Lg, M, mCmd, not_1_out, not_2_out, or_1_out, or_2_out,
       or_3_out, or_4_out, p, Res, S, Sg;
  wire [4:0] C5;
  wire [5:0] Con_1, Con_2, counter_2_count_6, Pinout;
  wire [31:0] buffer_1_out, buffer_4_out, buffer_7_out, buffer_58_out, buffer_65_out, horizctrl_1_out1_2, LY,
       memory_1_out_1, memory_1_out_2, memory_1_out_3, memory_1_out_4, memory_1_out_5, memory_1_out_6,
       memory_1_out_7, memory_1_out_8, memory_1_out_9, memory_1_out_10, memory_1_out_11, memory_1_out_12,
       memory_1_out_13, memory_1_out_14, memory_1_out_15, memory_1_out_16, memory_1_out_17, memory_1_out_18,
       memory_1_out_19, memory_1_out_20, memory_1_out_21, memory_1_out_22, memory_1_out_23, memory_1_out_24,
       memory_1_out_25, memory_1_out_26, memory_1_out_27, memory_1_out_28, memory_1_out_29, memory_1_out_30,
       memory_1_out_31, memory_1_out_32, memory_1_out_33, memory_1_out_34, memory_1_out_35, memory_1_out_36,
       memory_1_out_37, memory_1_out_38, memory_1_out_39, memory_1_out_40, memory_1_out_41, memory_1_out_42,
       memory_1_out_43, memory_1_out_44, memory_1_out_45, memory_1_out_46, memory_1_out_47, memory_1_out_48,
       memory_1_out_49, memory_1_out_50, memory_1_out_51, memory_1_out_52, memory_1_out_53, memory_1_out_54,
       memory_1_out_55, memory_1_out_56, memory_1_out_57, memory_1_out_58, memory_1_out_59, memory_1_out_60,
       memory_1_out_61, memory_1_out_62, memory_1_out_63, memory_1_out_64, X1, X2, XL1, XL2;

  DotMatrix #(.matrixcols(32), .matrixrows(1)) dotmatrix_1 (
    .col0(buffer_1_out[31]), .col1(buffer_1_out[30]), .col2(buffer_1_out[29]), .col3(buffer_1_out[28]),
    .col4(buffer_1_out[27]), .col5(buffer_1_out[26]), .col6(buffer_1_out[25]), .col7(buffer_1_out[24]),
    .col8(buffer_1_out[23]), .col9(buffer_1_out[22]), .col10(buffer_1_out[21]), .col11(buffer_1_out[20]),
    .col12(buffer_1_out[19]), .col13(buffer_1_out[18]), .col14(buffer_1_out[17]), .col15(buffer_1_out[16]),
    .col16(buffer_1_out[15]), .col17(buffer_1_out[14]), .col18(buffer_1_out[13]), .col19(buffer_1_out[12]),
    .col20(buffer_1_out[11]), .col21(buffer_1_out[10]), .col22(buffer_1_out[9]), .col23(buffer_1_out[8]),
    .col24(buffer_1_out[7]), .col25(buffer_1_out[6]), .col26(buffer_1_out[5]), .col27(buffer_1_out[4]),
    .col28(buffer_1_out[3]), .col29(buffer_1_out[2]), .col30(buffer_1_out[1]), .col31(buffer_1_out[0]));
  assign buffer_1_out = X1;  // Buffer buffer_1, 32 bits wide
  DotMatrix #(.matrixcols(32), .matrixrows(32)) dotmatrix_2 (
    .col0(memory_1_out_1), .col1(memory_1_out_2), .col2(memory_1_out_3), .col3(memory_1_out_4),
    .col4(memory_1_out_5), .col5(memory_1_out_6), .col6(memory_1_out_7), .col7(memory_1_out_8),
    .col8(memory_1_out_9), .col9(memory_1_out_10), .col10(memory_1_out_11), .col11(memory_1_out_12),
    .col12(memory_1_out_13), .col13(memory_1_out_14), .col14(memory_1_out_15), .col15(memory_1_out_16),
    .col16(memory_1_out_17), .col17(memory_1_out_18), .col18(memory_1_out_19), .col19(memory_1_out_20),
    .col20(memory_1_out_21), .col21(memory_1_out_22), .col22(memory_1_out_23), .col23(memory_1_out_24),
    .col24(memory_1_out_25), .col25(memory_1_out_26), .col26(memory_1_out_27), .col27(memory_1_out_28),
    .col28(memory_1_out_29), .col29(memory_1_out_30), .col30(memory_1_out_31), .col31(memory_1_out_32));
  DotMatrix #(.matrixcols(1), .matrixrows(32)) dotmatrix_3 (.col0(LY));
  Memory memory_1 (
    .Clock(or_1_out), .Reset(Res), .X_Location_1(XL1), .X_Location_2(XL2), .Y_Location(LY),
    .Out_1(memory_1_out_1), .Out_2(memory_1_out_2), .Out_3(memory_1_out_3), .Out_4(memory_1_out_4),
    .Out_5(memory_1_out_5), .Out_6(memory_1_out_6), .Out_7(memory_1_out_7), .Out_8(memory_1_out_8),
    .Out_9(memory_1_out_9), .Out_10(memory_1_out_10), .Out_11(memory_1_out_11), .Out_12(memory_1_out_12),
    .Out_13(memory_1_out_13), .Out_14(memory_1_out_14), .Out_15(memory_1_out_15), .Out_16(memory_1_out_16),
    .Out_17(memory_1_out_17), .Out_18(memory_1_out_18), .Out_19(memory_1_out_19), .Out_20(memory_1_out_20),
    .Out_21(memory_1_out_21), .Out_22(memory_1_out_22), .Out_23(memory_1_out_23), .Out_24(memory_1_out_24),
    .Out_25(memory_1_out_25), .Out_26(memory_1_out_26), .Out_27(memory_1_out_27), .Out_28(memory_1_out_28),
    .Out_29(memory_1_out_29), .Out_30(memory_1_out_30), .Out_31(memory_1_out_31), .Out_32(memory_1_out_32),
    .Out_33(memory_1_out_33), .Out_34(memory_1_out_34), .Out_35(memory_1_out_35), .Out_36(memory_1_out_36),
    .Out_37(memory_1_out_37), .Out_38(memory_1_out_38), .Out_39(memory_1_out_39), .Out_40(memory_1_out_40),
    .Out_41(memory_1_out_41), .Out_42(memory_1_out_42), .Out_43(memory_1_out_43), .Out_44(memory_1_out_44),
    .Out_45(memory_1_out_45), .Out_46(memory_1_out_46), .Out_47(memory_1_out_47), .Out_48(memory_1_out_48),
    .Out_49(memory_1_out_49), .Out_50(memory_1_out_50), .Out_51(memory_1_out_51), .Out_52(memory_1_out_52),
    .Out_53(memory_1_out_53), .Out_54(memory_1_out_54), .Out_55(memory_1_out_55), .Out_56(memory_1_out_56),
    .Out_57(memory_1_out_57), .Out_58(memory_1_out_58), .Out_59(memory_1_out_59), .Out_60(memory_1_out_60),
    .Out_61(memory_1_out_61), .Out_62(memory_1_out_62), .Out_63(memory_1_out_63), .Out_64(memory_1_out_64),
    .Draw(or_2_out), .Move(M), .Save(S), .Load(L), .Loading(Lg), .Saving(Sg), .Erase_memory(Er));
  not not_1 (not_1_out, Con_1[5]);
  or or_1 (or_1_out, Pinout[3], Pinout[2], Pinout[1], Pinout[0], p);
  LED Border (.in(Pinout[5]));
  Button button (.out(Pinout[3]));
  Button button_2 (.out(Pinout[2]));
  Demultiplexer #(.select(5), .width(32), .disabled(0)) demultiplexer_1 (
    .in(LY), .sel(Con_1[4:0]), .en(not_1_out));  // open: out0, out1, out2, out3, out4, out5, out6, out7, out8, out9, out10, out11, out12, out13, out14, out15, out16, out17, out18, out19, out20, out21, out22, out23, out24, out25, out26, out27, out28, out29, out30, out31
  assign XL1 = buffer_58_out;  // Buffer buffer_2, 32 bits wide
  buf buffer_3 (buffer_58_out[31], buffer_4_out[0]);
  assign buffer_4_out = X1;  // Buffer buffer_4, 32 bits wide
  assign XL2 = buffer_65_out;  // Buffer buffer_5, 32 bits wide
  buf buffer_6 (buffer_65_out[31], buffer_7_out[0]);
  assign buffer_7_out = X2;  // Buffer buffer_7, 32 bits wide
  Button Erase_RAM (.out(Er));
  LED led_1 (.in(drw));
  LED led_2 (.in(drw));
  Button Draw_or_Erase (.out(cmd));
  buf buffer_8 (buffer_58_out[26], buffer_4_out[5]);
  buf buffer_9 (buffer_58_out[29], buffer_4_out[2]);
  buf buffer_10 (buffer_58_out[27], buffer_4_out[4]);
  buf buffer_11 (buffer_58_out[30], buffer_4_out[1]);
  buf buffer_12 (buffer_58_out[24], buffer_4_out[7]);
  buf buffer_13 (buffer_58_out[25], buffer_4_out[6]);
  buf buffer_14 (buffer_58_out[23], buffer_4_out[8]);
  buf buffer_15 (buffer_58_out[28], buffer_4_out[3]);
  buf buffer_16 (buffer_65_out[29], buffer_7_out[2]);
  buf buffer_17 (buffer_65_out[26], buffer_7_out[5]);
  buf buffer_18 (buffer_65_out[27], buffer_7_out[4]);
  buf buffer_19 (buffer_65_out[25], buffer_7_out[6]);
  buf buffer_20 (buffer_65_out[23], buffer_7_out[8]);
  buf buffer_21 (buffer_65_out[30], buffer_7_out[1]);
  buf buffer_22 (buffer_65_out[24], buffer_7_out[7]);
  buf buffer_23 (buffer_65_out[28], buffer_7_out[3]);
  DotMatrix #(.matrixcols(32), .matrixrows(1)) dotmatrix_4 (
    .col0(X2[31]), .col1(X2[30]), .col2(X2[29]), .col3(X2[28]), .col4(X2[27]), .col5(X2[26]), .col6(X2[25]),
    .col7(X2[24]), .col8(X2[23]), .col9(X2[22]), .col10(X2[21]), .col11(X2[20]), .col12(X2[19]),
    .col13(X2[18]), .col14(X2[17]), .col15(X2[16]), .col16(X2[15]), .col17(X2[14]), .col18(X2[13]),
    .col19(X2[12]), .col20(X2[11]), .col21(X2[10]), .col22(X2[9]), .col23(X2[8]), .col24(X2[7]),
    .col25(X2[6]), .col26(X2[5]), .col27(X2[4]), .col28(X2[3]), .col29(X2[2]), .col30(X2[1]), .col31(X2[0]));
  DotMatrix #(.matrixcols(32), .matrixrows(32)) dotmatrix_5 (
    .col0(memory_1_out_33), .col1(memory_1_out_34), .col2(memory_1_out_35), .col3(memory_1_out_36),
    .col4(memory_1_out_37), .col5(memory_1_out_38), .col6(memory_1_out_39), .col7(memory_1_out_40),
    .col8(memory_1_out_41), .col9(memory_1_out_42), .col10(memory_1_out_43), .col11(memory_1_out_44),
    .col12(memory_1_out_45), .col13(memory_1_out_46), .col14(memory_1_out_47), .col15(memory_1_out_48),
    .col16(memory_1_out_49), .col17(memory_1_out_50), .col18(memory_1_out_51), .col19(memory_1_out_52),
    .col20(memory_1_out_53), .col21(memory_1_out_54), .col22(memory_1_out_55), .col23(memory_1_out_56),
    .col24(memory_1_out_57), .col25(memory_1_out_58), .col26(memory_1_out_59), .col27(memory_1_out_60),
    .col28(memory_1_out_61), .col29(memory_1_out_62), .col30(memory_1_out_63), .col31(memory_1_out_64));
  Button Force_Print (.out(p));
  Button Reset (.out(Res));
  not not_2 (not_2_out, Con_2[5]);
  buf buffer_24 (buffer_58_out[15], buffer_4_out[16]);
  buf buffer_25 (buffer_58_out[16], buffer_4_out[15]);
  buf buffer_26 (buffer_58_out[20], buffer_4_out[11]);
  buf buffer_27 (buffer_58_out[18], buffer_4_out[13]);
  buf buffer_28 (buffer_58_out[21], buffer_4_out[10]);
  buf buffer_29 (buffer_58_out[17], buffer_4_out[14]);
  buf buffer_30 (buffer_58_out[22], buffer_4_out[9]);
  buf buffer_31 (buffer_58_out[19], buffer_4_out[12]);
  buf buffer_32 (buffer_65_out[15], buffer_7_out[16]);
  buf buffer_33 (buffer_65_out[17], buffer_7_out[14]);
  buf buffer_34 (buffer_65_out[19], buffer_7_out[12]);
  buf buffer_35 (buffer_65_out[21], buffer_7_out[10]);
  buf buffer_36 (buffer_65_out[20], buffer_7_out[11]);
  buf buffer_37 (buffer_65_out[16], buffer_7_out[15]);
  buf buffer_38 (buffer_65_out[22], buffer_7_out[9]);
  buf buffer_39 (buffer_65_out[18], buffer_7_out[13]);
  LED led_3 (.in(Lg));
  LED led_4 (.in(Sg));
  Button Load (.out(L));
  Button Save (.out(S));
  LED led_5 (.in(M));
  LED led_6 (.in(M));
  Button Move_cursor (.out(mCmd));
  buf buffer_40 (buffer_58_out[8], buffer_4_out[23]);
  buf buffer_41 (buffer_58_out[14], buffer_4_out[17]);
  buf buffer_42 (buffer_58_out[11], buffer_4_out[20]);
  buf buffer_43 (buffer_58_out[7], buffer_4_out[24]);
  buf buffer_44 (buffer_58_out[9], buffer_4_out[22]);
  buf buffer_45 (buffer_58_out[12], buffer_4_out[19]);
  buf buffer_46 (buffer_58_out[10], buffer_4_out[21]);
  buf buffer_47 (buffer_58_out[13], buffer_4_out[18]);
  buf buffer_48 (buffer_65_out[14], buffer_7_out[17]);
  buf buffer_49 (buffer_65_out[8], buffer_7_out[23]);
  buf buffer_50 (buffer_65_out[13], buffer_7_out[18]);
  buf buffer_51 (buffer_65_out[11], buffer_7_out[20]);
  buf buffer_52 (buffer_65_out[10], buffer_7_out[21]);
  buf buffer_53 (buffer_65_out[12], buffer_7_out[19]);
  buf buffer_54 (buffer_65_out[9], buffer_7_out[22]);
  buf buffer_55 (buffer_65_out[7], buffer_7_out[24]);
  Button button_3 (.out(Pinout[1]));
  Button v (.out(Pinout[0]));
  Demultiplexer #(.select(5), .width(32), .disabled(0)) demultiplexer_2 (
    .in(LY), .sel(Con_2[4:0]), .en(not_2_out));  // open: out0, out1, out2, out3, out4, out5, out6, out7, out8, out9, out10, out11, out12, out13, out14, out15, out16, out17, out18, out19, out20, out21, out22, out23, out24, out25, out26, out27, out28, out29, out30, out31
  buf buffer_56 (buffer_58_out[6], buffer_4_out[25]);
  buf buffer_57 (buffer_58_out[1], buffer_4_out[30]);
  buf buffer_58 (buffer_58_out[0], buffer_4_out[31]);
  buf buffer_59 (buffer_58_out[2], buffer_4_out[29]);
  buf buffer_60 (buffer_58_out[4], buffer_4_out[27]);
  buf buffer_61 (buffer_58_out[3], buffer_4_out[28]);
  buf buffer_62 (buffer_58_out[5], buffer_4_out[26]);
  buf buffer_63 (buffer_65_out[1], buffer_7_out[30]);
  buf buffer_64 (buffer_65_out[4], buffer_7_out[27]);
  buf buffer_65 (buffer_65_out[0], buffer_7_out[31]);
  buf buffer_66 (buffer_65_out[6], buffer_7_out[25]);
  buf buffer_67 (buffer_65_out[2], buffer_7_out[29]);
  buf buffer_68 (buffer_65_out[3], buffer_7_out[28]);
  buf buffer_69 (buffer_65_out[5], buffer_7_out[26]);
  or or_2 (or_2_out, p, drw);
  LED Border_2 (.in(Pinout[4]));
  vertCtrl vertctrl_1 (.Count(C5), .Out(LY));
  counter counter_1 (
    .Double(1'b0), .Count_5(C5), .Led(counter_1_led), .Lower_Button(Pinout[1]), .Raise_Button(Pinout[0]));  // open: Count_6
  and and_1 (Pinout[4], or_3_out, counter_1_led);
  or or_3 (or_3_out, Pinout[0], Pinout[1]);
  horizCtrl horizctrl_1 (
    .Count(counter_2_count_6), .Out1(X2), .Out1_2(horizctrl_1_out1_2), .Con_1(Con_1), .Con_2(Con_2));
  counter counter_2 (
    .Double(1'b1), .Count_6(counter_2_count_6), .Led(counter_2_led), .Lower_Button(Pinout[3]),
    .Raise_Button(Pinout[2]));  // open: Count_5
  or or_4 (or_4_out, Pinout[2], Pinout[3]);
  and and_2 (Pinout[5], or_4_out, counter_2_led);
  T_Flip_Flop t_ff_1 (.clk(cmd), .T(cmd), .Q(drw));  // open: Qn, preset, reset, en
  T_Flip_Flop t_ff_2 (.clk(mCmd), .T(mCmd), .Q(M));  // open: Qn, preset, reset, en
  assign X1 = horizctrl_1_out1_2;  // Buffer buffer_70, 32 bits wide

  // Other names for the same wires on the sheet: Y[31:0] = LY

  // Notes on the sheet:
  //   Overrides draw and
  //   erase commands
endmodule

module horizCtrl (
  input  [5:0] Count,
  output [5:0] Con_2,
  output [5:0] Con_1,
  output [31:0] Out1,
  output [31:0] Out1_2
);

  wire not_1_out, not_2_out, not_3_out, not_4_out, not_5_out;
  wire [4:0] buffer_1_out, buffer_6_out, controlled_buffer_5_out, controlled_buffer_6_out;
  wire [5:0] bit_extender_1_out, bit_extender_2_out;
  wire [31:0] demultiplexer_1_out31, demultiplexer_2_out31;

  assign Con_2 = not_2_out ? 6'b100000 : 6'bz;  // Controlled_Buffer controlled_buffer_1
  assign Con_2 = not_3_out ? bit_extender_1_out : 6'bz;  // Controlled_Buffer controlled_buffer_2
  assign bit_extender_1_out = {{1{1'b0}}, buffer_6_out};  // Bit_Extender bit_extender_1
  assign Con_1 = not_3_out ? 6'b100000 : 6'bz;  // Controlled_Buffer controlled_buffer_3
  assign Con_1 = not_1_out ? bit_extender_2_out : 6'bz;  // Controlled_Buffer controlled_buffer_4
  assign bit_extender_2_out = {{1{1'b0}}, buffer_1_out};  // Bit_Extender bit_extender_2
  assign controlled_buffer_5_out = not_1_out ? buffer_1_out : 5'bz;  // Controlled_Buffer controlled_buffer_5
  buf buffer_1 (buffer_1_out[0], Count[0]);
  buf buffer_2 (buffer_1_out[1], Count[1]);
  not not_1 (not_1_out, Count[5]);
  buf buffer_3 (buffer_1_out[2], Count[2]);
  buf buffer_4 (buffer_1_out[3], Count[3]);
  buf buffer_5 (buffer_1_out[4], Count[4]);
  buf buffer_6 (buffer_6_out[0], Count[0]);
  buf buffer_7 (buffer_6_out[1], Count[1]);
  buf buffer_8 (buffer_6_out[2], Count[2]);
  buf buffer_9 (buffer_6_out[3], Count[3]);
  buf buffer_10 (buffer_6_out[4], Count[4]);
  assign controlled_buffer_6_out = Count[5] ? buffer_6_out : 5'bz;  // Controlled_Buffer controlled_buffer_6
  assign Out1_2 = not_1_out ? demultiplexer_1_out31 : 32'bz;  // Controlled_Buffer controlled_buffer_7
  assign Out1_2 = Count[5] ? {32{1'b0}} : 32'bz;  // Controlled_Buffer controlled_buffer_8
  not not_2 (not_2_out, not_3_out);
  not not_3 (not_3_out, not_1_out);
  Demultiplexer #(.select(5)) demultiplexer_1 (
    .out0(demultiplexer_1_out31[31]), .out1(demultiplexer_1_out31[30]), .out2(demultiplexer_1_out31[29]),
    .out3(demultiplexer_1_out31[28]), .out4(demultiplexer_1_out31[27]), .out5(demultiplexer_1_out31[26]),
    .out6(demultiplexer_1_out31[25]), .out7(demultiplexer_1_out31[24]), .out8(demultiplexer_1_out31[23]),
    .out9(demultiplexer_1_out31[22]), .out10(demultiplexer_1_out31[21]), .out11(demultiplexer_1_out31[20]),
    .out12(demultiplexer_1_out31[19]), .out13(demultiplexer_1_out31[18]), .out14(demultiplexer_1_out31[17]),
    .out15(demultiplexer_1_out31[16]), .out16(demultiplexer_1_out31[15]), .out17(demultiplexer_1_out31[14]),
    .out18(demultiplexer_1_out31[13]), .out19(demultiplexer_1_out31[12]), .out20(demultiplexer_1_out31[11]),
    .out21(demultiplexer_1_out31[10]), .out22(demultiplexer_1_out31[9]), .out23(demultiplexer_1_out31[8]),
    .out24(demultiplexer_1_out31[7]), .out25(demultiplexer_1_out31[6]), .out26(demultiplexer_1_out31[5]),
    .out27(demultiplexer_1_out31[4]), .out28(demultiplexer_1_out31[3]), .out29(demultiplexer_1_out31[2]),
    .out30(demultiplexer_1_out31[1]), .out31(demultiplexer_1_out31[0]), .in(1'b1),
    .sel(controlled_buffer_5_out));  // open: en
  not not_4 (not_4_out, Count[5]);
  Demultiplexer #(.select(5)) demultiplexer_2 (
    .out0(demultiplexer_2_out31[31]), .out1(demultiplexer_2_out31[30]), .out2(demultiplexer_2_out31[29]),
    .out3(demultiplexer_2_out31[28]), .out4(demultiplexer_2_out31[27]), .out5(demultiplexer_2_out31[26]),
    .out6(demultiplexer_2_out31[25]), .out7(demultiplexer_2_out31[24]), .out8(demultiplexer_2_out31[23]),
    .out9(demultiplexer_2_out31[22]), .out10(demultiplexer_2_out31[21]), .out11(demultiplexer_2_out31[20]),
    .out12(demultiplexer_2_out31[19]), .out13(demultiplexer_2_out31[18]), .out14(demultiplexer_2_out31[17]),
    .out15(demultiplexer_2_out31[16]), .out16(demultiplexer_2_out31[15]), .out17(demultiplexer_2_out31[14]),
    .out18(demultiplexer_2_out31[13]), .out19(demultiplexer_2_out31[12]), .out20(demultiplexer_2_out31[11]),
    .out21(demultiplexer_2_out31[10]), .out22(demultiplexer_2_out31[9]), .out23(demultiplexer_2_out31[8]),
    .out24(demultiplexer_2_out31[7]), .out25(demultiplexer_2_out31[6]), .out26(demultiplexer_2_out31[5]),
    .out27(demultiplexer_2_out31[4]), .out28(demultiplexer_2_out31[3]), .out29(demultiplexer_2_out31[2]),
    .out30(demultiplexer_2_out31[1]), .out31(demultiplexer_2_out31[0]), .in(1'b1),
    .sel(controlled_buffer_6_out));  // open: en
  assign Out1 = not_5_out ? demultiplexer_2_out31 : 32'bz;  // Controlled_Buffer controlled_buffer_9
  assign Out1 = not_4_out ? {32{1'b0}} : 32'bz;  // Controlled_Buffer controlled_buffer_10
  not not_5 (not_5_out, not_4_out);
endmodule

module vertCtrl (
  input  [4:0] Count,
  output [31:0] Out
);

  wire [4:0] buffer_1_out;

  buf buffer_1 (buffer_1_out[0], Count[0]);
  buf buffer_2 (buffer_1_out[1], Count[1]);
  buf buffer_3 (buffer_1_out[2], Count[2]);
  buf buffer_4 (buffer_1_out[3], Count[3]);
  buf buffer_5 (buffer_1_out[4], Count[4]);
  Demultiplexer #(.select(5)) demultiplexer_1 (
    .out0(Out[31]), .out1(Out[30]), .out2(Out[29]), .out3(Out[28]), .out4(Out[27]), .out5(Out[26]),
    .out6(Out[25]), .out7(Out[24]), .out8(Out[23]), .out9(Out[22]), .out10(Out[21]), .out11(Out[20]),
    .out12(Out[19]), .out13(Out[18]), .out14(Out[17]), .out15(Out[16]), .out16(Out[15]), .out17(Out[14]),
    .out18(Out[13]), .out19(Out[12]), .out20(Out[11]), .out21(Out[10]), .out22(Out[9]), .out23(Out[8]),
    .out24(Out[7]), .out25(Out[6]), .out26(Out[5]), .out27(Out[4]), .out28(Out[3]), .out29(Out[2]),
    .out30(Out[1]), .out31(Out[0]), .in(1'b1), .sel(buffer_1_out));  // open: en
endmodule

module counter (
  input  Double,
  input  Lower_Button,
  input  Raise_Button,
  output [4:0] Count_5,
  output [5:0] Count_6,
  output Led
);

  wire and_1_out, and_2_out, ap, counter_1_carry, counter_2_carry, ndbl;

  not not_1 (ndbl, Double);
  Counter #(.width(5), .max('h1f), .ongoal("stay")) counter_1 (
    .load(Lower_Button), .count(ap), .Q(Count_5), .carry(counter_1_carry), .clk(ap));  // open: D, clr
  Counter #(.width(6), .max('h3f), .ongoal("stay")) counter_2 (
    .load(Lower_Button), .count(ap), .Q(Count_6), .carry(counter_2_carry), .clk(ap));  // open: D, clr
  and and_1 (and_1_out, counter_2_carry, Double);
  or or_1 (ap, Raise_Button, Lower_Button);
  and and_2 (and_2_out, counter_1_carry, ndbl);
  assign ap = Raise_Button ? Raise_Button : 1'bz;  // Controlled_Buffer controlled_buffer_1
  assign ap = Lower_Button ? Lower_Button : 1'bz;  // Controlled_Buffer controlled_buffer_2
  or or_2 (Led, and_2_out, and_1_out);

  // Other names for the same wires on the sheet: dbl = Double; lwr = Lower_Button
endmodule

module Memory (
  input  Erase_memory,
  input  Load,
  input  Save,
  input  Move,
  input  Draw,
  input  Clock,
  input  Reset,
  input  [31:0] X_Location_1,
  input  [31:0] X_Location_2,
  input  [31:0] Y_Location,
  output Loading,
  output [31:0] Out_1,
  output [31:0] Out_2,
  output [31:0] Out_3,
  output Saving,
  output [31:0] Out_4,
  output [31:0] Out_5,
  output [31:0] Out_6,
  output [31:0] Out_7,
  output [31:0] Out_8,
  output [31:0] Out_9,
  output [31:0] Out_10,
  output [31:0] Out_11,
  output [31:0] Out_12,
  output [31:0] Out_13,
  output [31:0] Out_14,
  output [31:0] Out_15,
  output [31:0] Out_16,
  output [31:0] Out_17,
  output [31:0] Out_18,
  output [31:0] Out_19,
  output [31:0] Out_20,
  output [31:0] Out_21,
  output [31:0] Out_22,
  output [31:0] Out_23,
  output [31:0] Out_24,
  output [31:0] Out_25,
  output [31:0] Out_26,
  output [31:0] Out_27,
  output [31:0] Out_28,
  output [31:0] Out_29,
  output [31:0] Out_30,
  output [31:0] Out_31,
  output [31:0] Out_32,
  output [31:0] Out_33,
  output [31:0] Out_34,
  output [31:0] Out_35,
  output [31:0] Out_36,
  output [31:0] Out_37,
  output [31:0] Out_38,
  output [31:0] Out_39,
  output [31:0] Out_40,
  output [31:0] Out_41,
  output [31:0] Out_42,
  output [31:0] Out_43,
  output [31:0] Out_44,
  output [31:0] Out_45,
  output [31:0] Out_46,
  output [31:0] Out_47,
  output [31:0] Out_48,
  output [31:0] Out_49,
  output [31:0] Out_50,
  output [31:0] Out_51,
  output [31:0] Out_52,
  output [31:0] Out_53,
  output [31:0] Out_54,
  output [31:0] Out_55,
  output [31:0] Out_56,
  output [31:0] Out_57,
  output [31:0] Out_58,
  output [31:0] Out_59,
  output [31:0] Out_60,
  output [31:0] Out_61,
  output [31:0] Out_62,
  output [31:0] Out_63,
  output [31:0] Out_64
);

  wire and_1_out, and_2_out, and_3_out, and_4_out, and_5_out, and_6_out, bitfinder_1_found,
       bitfinder_2_found, C, Cl, clock_1_out, counter_1_carry, decoder_1_out0, decoder_1_out1,
       decoder_1_out2, decoder_1_out3, decoder_1_out4, decoder_1_out5, decoder_1_out6, decoder_1_out7,
       decoder_1_out8, decoder_1_out9, decoder_1_out10, decoder_1_out11, decoder_1_out12, decoder_1_out13,
       decoder_1_out14, decoder_1_out15, decoder_1_out16, decoder_1_out17, decoder_1_out18, decoder_1_out19,
       decoder_1_out20, decoder_1_out21, decoder_1_out22, decoder_1_out23, decoder_1_out24, decoder_1_out25,
       decoder_1_out26, decoder_1_out27, decoder_1_out28, decoder_1_out29, decoder_1_out30, decoder_1_out31,
       decoder_2_out0, decoder_2_out1, decoder_2_out2, decoder_2_out3, decoder_2_out4, decoder_2_out5,
       decoder_2_out6, decoder_2_out7, decoder_2_out8, decoder_2_out9, decoder_2_out10, decoder_2_out11,
       decoder_2_out12, decoder_2_out13, decoder_2_out14, decoder_2_out15, decoder_2_out16, decoder_2_out17,
       decoder_2_out18, decoder_2_out19, decoder_2_out20, decoder_2_out21, decoder_2_out22, decoder_2_out23,
       decoder_2_out24, decoder_2_out25, decoder_2_out26, decoder_2_out27, decoder_2_out28, decoder_2_out29,
       decoder_2_out30, decoder_2_out31, decoder_3_out0, decoder_3_out1, decoder_3_out2, decoder_3_out3,
       decoder_3_out4, decoder_3_out5, decoder_3_out6, decoder_3_out7, decoder_3_out8, decoder_3_out9,
       decoder_3_out10, decoder_3_out11, decoder_3_out12, decoder_3_out13, decoder_3_out14, decoder_3_out15,
       decoder_3_out16, decoder_3_out17, decoder_3_out18, decoder_3_out19, decoder_3_out20, decoder_3_out21,
       decoder_3_out22, decoder_3_out23, decoder_3_out24, decoder_3_out25, decoder_3_out26, decoder_3_out27,
       decoder_3_out28, decoder_3_out29, decoder_3_out30, decoder_3_out31, decoder_4_out0, decoder_4_out1,
       decoder_4_out2, decoder_4_out3, decoder_4_out4, decoder_4_out5, decoder_4_out6, decoder_4_out7,
       decoder_4_out8, decoder_4_out9, decoder_4_out10, decoder_4_out11, decoder_4_out12, decoder_4_out13,
       decoder_4_out14, decoder_4_out15, decoder_4_out16, decoder_4_out17, decoder_4_out18, decoder_4_out19,
       decoder_4_out20, decoder_4_out21, decoder_4_out22, decoder_4_out23, decoder_4_out24, decoder_4_out25,
       decoder_4_out26, decoder_4_out27, decoder_4_out28, decoder_4_out29, decoder_4_out30, decoder_4_out31,
       dreg_1_out_clear, dreg_1_out_draw, dreg_2_out_clear, dreg_2_out_draw, dreg_3_out_clear,
       dreg_3_out_draw, dreg_4_out_clear, dreg_4_out_draw, dreg_5_out_clear, dreg_5_out_draw,
       dreg_6_out_clear, dreg_6_out_draw, dreg_7_out_clear, dreg_7_out_draw, dreg_8_out_clear,
       dreg_8_out_draw, dreg_9_out_clear, dreg_9_out_draw, dreg_10_out_clear, dreg_10_out_draw,
       dreg_11_out_clear, dreg_11_out_draw, dreg_12_out_clear, dreg_12_out_draw, dreg_13_out_clear,
       dreg_13_out_draw, dreg_14_out_clear, dreg_14_out_draw, dreg_15_out_clear, dreg_15_out_draw,
       dreg_16_out_clear, dreg_16_out_draw, dreg_17_out_clear, dreg_17_out_draw, dreg_18_out_clear,
       dreg_18_out_draw, dreg_19_out_clear, dreg_19_out_draw, dreg_20_out_clear, dreg_20_out_draw,
       dreg_21_out_clear, dreg_21_out_draw, dreg_22_out_clear, dreg_22_out_draw, dreg_23_out_clear,
       dreg_23_out_draw, dreg_24_out_clear, dreg_24_out_draw, dreg_25_out_clear, dreg_25_out_draw,
       dreg_26_out_clear, dreg_26_out_draw, dreg_27_out_clear, dreg_27_out_draw, dreg_28_out_clear,
       dreg_28_out_draw, dreg_29_out_clear, dreg_29_out_draw, dreg_30_out_clear, dreg_30_out_draw,
       dreg_31_out_clear, dreg_31_out_draw, dreg_32_out_clear, dreg_32_out_draw, dreg_33_out_clear,
       dreg_33_out_draw, dreg_34_out_clear, dreg_34_out_draw, dreg_35_out_clear, dreg_35_out_draw,
       dreg_36_out_clear, dreg_36_out_draw, dreg_37_out_clear, dreg_37_out_draw, dreg_38_out_clear,
       dreg_38_out_draw, dreg_39_out_clear, dreg_39_out_draw, dreg_40_out_clear, dreg_40_out_draw,
       dreg_41_out_clear, dreg_41_out_draw, dreg_42_out_clear, dreg_42_out_draw, dreg_43_out_clear,
       dreg_43_out_draw, dreg_44_out_clear, dreg_44_out_draw, dreg_45_out_clear, dreg_45_out_draw,
       dreg_46_out_clear, dreg_46_out_draw, dreg_47_out_clear, dreg_47_out_draw, dreg_48_out_clear,
       dreg_48_out_draw, dreg_49_out_clear, dreg_49_out_draw, dreg_50_out_clear, dreg_50_out_draw,
       dreg_51_out_clear, dreg_51_out_draw, dreg_52_out_clear, dreg_52_out_draw, dreg_53_out_clear,
       dreg_53_out_draw, dreg_54_out_clear, dreg_54_out_draw, dreg_55_out_clear, dreg_55_out_draw,
       dreg_56_out_clear, dreg_56_out_draw, dreg_57_out_clear, dreg_57_out_draw, dreg_58_out_clear,
       dreg_58_out_draw, dreg_59_out_clear, dreg_59_out_draw, dreg_60_out_clear, dreg_60_out_draw,
       dreg_61_out_clear, dreg_61_out_draw, dreg_62_out_clear, dreg_62_out_draw, dreg_63_out_clear,
       dreg_63_out_draw, dreg_64_out_clear, dreg_64_out_draw, not_2_out, nreg_1_out_button, nreg_1_out_clear,
       nreg_2_out_button, nreg_2_out_clear, nreg_3_out_button, nreg_3_out_clear, nreg_4_out_button,
       nreg_4_out_clear, nreg_5_out_button, nreg_5_out_clear, nreg_6_out_button, nreg_6_out_clear,
       nreg_7_out_button, nreg_7_out_clear, nreg_8_out_button, nreg_8_out_clear, nreg_9_out_button,
       nreg_9_out_clear, nreg_10_out_button, nreg_10_out_clear, nreg_11_out_button, nreg_11_out_clear,
       nreg_12_out_button, nreg_12_out_clear, nreg_13_out_button, nreg_13_out_clear, nreg_14_out_button,
       nreg_14_out_clear, nreg_15_out_button, nreg_15_out_clear, nreg_16_out_button, nreg_16_out_clear,
       nreg_17_out_button, nreg_17_out_clear, nreg_18_out_button, nreg_18_out_clear, nreg_19_out_button,
       nreg_19_out_clear, nreg_20_out_button, nreg_20_out_clear, nreg_21_out_button, nreg_21_out_clear,
       nreg_22_out_button, nreg_22_out_clear, nreg_23_out_button, nreg_23_out_clear, nreg_24_out_button,
       nreg_24_out_clear, nreg_25_out_button, nreg_25_out_clear, nreg_26_out_button, nreg_26_out_clear,
       nreg_27_out_button, nreg_27_out_clear, nreg_28_out_button, nreg_28_out_clear, nreg_29_out_button,
       nreg_29_out_clear, nreg_30_out_button, nreg_30_out_clear, nreg_31_out_button, nreg_31_out_clear,
       or_1_out, or_2_out, or_3_out, or_4_out, or_5_out, or_6_out, undriven, undriven_2, undriven_3,
       undriven_4, undriven_5, undriven_6, undriven_7, undriven_8, undriven_9, undriven_10, undriven_11,
       undriven_12, undriven_13, undriven_14, undriven_15, undriven_16, undriven_17, undriven_18,
       undriven_19, undriven_20, undriven_21, undriven_22, undriven_23, undriven_24, undriven_25,
       undriven_26, undriven_27, undriven_28, undriven_29, undriven_30, undriven_31, undriven_32,
       undriven_33, undriven_34, undriven_35, undriven_36, undriven_37, undriven_38, undriven_39,
       undriven_40, undriven_41, undriven_42, undriven_43, undriven_44, undriven_45, undriven_46,
       undriven_47, undriven_48, undriven_49, undriven_50, undriven_51, undriven_52, undriven_53,
       undriven_54, undriven_55, undriven_56, undriven_57, undriven_58, undriven_59, undriven_60,
       undriven_61, undriven_62, undriven_63, undriven_64, undriven_65, undriven_66, undriven_67,
       undriven_68, undriven_69, undriven_70, undriven_71, undriven_72, undriven_73, undriven_74,
       undriven_75, undriven_76, undriven_77, undriven_78, undriven_79, undriven_80, undriven_81,
       undriven_82, undriven_83, undriven_84, undriven_85, undriven_86, undriven_87, undriven_88,
       undriven_89, undriven_90, undriven_91, undriven_92, undriven_93, undriven_94, undriven_95,
       undriven_96, undriven_97, undriven_98, undriven_99, undriven_100, undriven_101, undriven_102,
       undriven_103, undriven_104, undriven_105, undriven_106, undriven_107, undriven_108, undriven_109,
       undriven_110, undriven_111, undriven_112, undriven_113, undriven_114, undriven_115, undriven_116,
       undriven_117, undriven_118, undriven_119, undriven_120, undriven_121, undriven_122, undriven_123,
       undriven_124, undriven_125, undriven_126, undriven_127, undriven_128;
  wire [4:0] bitfinder_1_index, bitfinder_2_index, CA;
  wire [31:0] CD1, CD2, demultiplexer_1_out0, demultiplexer_1_out1, demultiplexer_1_out2,
       demultiplexer_1_out3, demultiplexer_1_out4, demultiplexer_1_out5, demultiplexer_1_out6,
       demultiplexer_1_out7, demultiplexer_1_out8, demultiplexer_1_out9, demultiplexer_1_out10,
       demultiplexer_1_out11, demultiplexer_1_out12, demultiplexer_1_out13, demultiplexer_1_out14,
       demultiplexer_1_out15, demultiplexer_1_out16, demultiplexer_1_out17, demultiplexer_1_out18,
       demultiplexer_1_out19, demultiplexer_1_out20, demultiplexer_1_out21, demultiplexer_1_out22,
       demultiplexer_1_out23, demultiplexer_1_out24, demultiplexer_1_out25, demultiplexer_1_out26,
       demultiplexer_1_out27, demultiplexer_1_out28, demultiplexer_1_out29, demultiplexer_1_out30,
       demultiplexer_1_out31, demultiplexer_2_out0, demultiplexer_2_out1, demultiplexer_2_out2,
       demultiplexer_2_out3, demultiplexer_2_out4, demultiplexer_2_out5, demultiplexer_2_out6,
       demultiplexer_2_out7, demultiplexer_2_out8, demultiplexer_2_out9, demultiplexer_2_out10,
       demultiplexer_2_out11, demultiplexer_2_out12, demultiplexer_2_out13, demultiplexer_2_out14,
       demultiplexer_2_out15, demultiplexer_2_out16, demultiplexer_2_out17, demultiplexer_2_out18,
       demultiplexer_2_out19, demultiplexer_2_out20, demultiplexer_2_out21, demultiplexer_2_out22,
       demultiplexer_2_out23, demultiplexer_2_out24, demultiplexer_2_out25, demultiplexer_2_out26,
       demultiplexer_2_out27, demultiplexer_2_out28, demultiplexer_2_out29, demultiplexer_2_out30,
       demultiplexer_2_out31, dreg_1_out_input, dreg_2_out_input, dreg_3_out_input, dreg_4_out_input,
       dreg_5_out_input, dreg_6_out_input, dreg_7_out_input, dreg_8_out_input, dreg_9_out_input,
       dreg_10_out_input, dreg_11_out_input, dreg_12_out_input, dreg_13_out_input, dreg_14_out_input,
       dreg_15_out_input, dreg_16_out_input, dreg_17_out_input, dreg_18_out_input, dreg_19_out_input,
       dreg_20_out_input, dreg_21_out_input, dreg_22_out_input, dreg_23_out_input, dreg_24_out_input,
       dreg_25_out_input, dreg_26_out_input, dreg_27_out_input, dreg_28_out_input, dreg_29_out_input,
       dreg_30_out_input, dreg_31_out_input, dreg_32_out_input, dreg_33_out_input, dreg_34_out_input,
       dreg_35_out_input, dreg_36_out_input, dreg_37_out_input, dreg_38_out_input, dreg_39_out_input,
       dreg_40_out_input, dreg_41_out_input, dreg_42_out_input, dreg_43_out_input, dreg_44_out_input,
       dreg_45_out_input, dreg_46_out_input, dreg_47_out_input, dreg_48_out_input, dreg_49_out_input,
       dreg_50_out_input, dreg_51_out_input, dreg_52_out_input, dreg_53_out_input, dreg_54_out_input,
       dreg_55_out_input, dreg_56_out_input, dreg_57_out_input, dreg_58_out_input, dreg_59_out_input,
       dreg_60_out_input, dreg_61_out_input, dreg_62_out_input, dreg_63_out_input, dreg_64_out_input,
       multiplexer_1_out, multiplexer_2_out, nreg_1_out_input, nreg_2_out_input, nreg_3_out_input,
       nreg_4_out_input, nreg_5_out_input, nreg_6_out_input, nreg_7_out_input, nreg_8_out_input,
       nreg_9_out_input, nreg_10_out_input, nreg_11_out_input, nreg_12_out_input, nreg_13_out_input,
       nreg_14_out_input, nreg_15_out_input, nreg_16_out_input, nreg_17_out_input, nreg_18_out_input,
       nreg_19_out_input, nreg_20_out_input, nreg_21_out_input, nreg_22_out_input, nreg_23_out_input,
       nreg_24_out_input, nreg_25_out_input, nreg_26_out_input, nreg_27_out_input, nreg_28_out_input,
       nreg_29_out_input, nreg_30_out_input, nreg_31_out_input, Y;

  nReg nreg_1 (
    .Out_Clear(nreg_1_out_clear), .Out_Button(nreg_1_out_button), .Out_Input(nreg_1_out_input));  // open: Enabled, Clear, Button, Input, Output
  nReg nreg_2 (
    .Clear(nreg_1_out_clear), .Button(nreg_1_out_button), .Input(nreg_1_out_input),
    .Out_Clear(nreg_2_out_clear), .Out_Button(nreg_2_out_button), .Out_Input(nreg_2_out_input));  // open: Enabled, Output
  nReg nreg_3 (
    .Clear(nreg_2_out_clear), .Button(nreg_2_out_button), .Input(nreg_2_out_input),
    .Out_Clear(nreg_3_out_clear), .Out_Button(nreg_3_out_button), .Out_Input(nreg_3_out_input));  // open: Enabled, Output
  nReg nreg_4 (
    .Clear(nreg_3_out_clear), .Button(nreg_3_out_button), .Input(nreg_3_out_input),
    .Out_Clear(nreg_4_out_clear), .Out_Button(nreg_4_out_button), .Out_Input(nreg_4_out_input));  // open: Enabled, Output
  nReg nreg_5 (
    .Clear(nreg_4_out_clear), .Button(nreg_4_out_button), .Input(nreg_4_out_input),
    .Out_Clear(nreg_5_out_clear), .Out_Button(nreg_5_out_button), .Out_Input(nreg_5_out_input));  // open: Enabled, Output
  nReg nreg_6 (
    .Clear(nreg_5_out_clear), .Button(nreg_5_out_button), .Input(nreg_5_out_input),
    .Out_Clear(nreg_6_out_clear), .Out_Button(nreg_6_out_button), .Out_Input(nreg_6_out_input));  // open: Enabled, Output
  nReg nreg_7 (
    .Clear(nreg_6_out_clear), .Button(nreg_6_out_button), .Input(nreg_6_out_input),
    .Out_Clear(nreg_7_out_clear), .Out_Button(nreg_7_out_button), .Out_Input(nreg_7_out_input));  // open: Enabled, Output
  nReg nreg_8 (
    .Clear(nreg_7_out_clear), .Button(nreg_7_out_button), .Input(nreg_7_out_input),
    .Out_Clear(nreg_8_out_clear), .Out_Button(nreg_8_out_button), .Out_Input(nreg_8_out_input));  // open: Enabled, Output
  nReg nreg_9 (
    .Clear(nreg_8_out_clear), .Button(nreg_8_out_button), .Input(nreg_8_out_input),
    .Out_Clear(nreg_9_out_clear), .Out_Button(nreg_9_out_button), .Out_Input(nreg_9_out_input));  // open: Enabled, Output
  nReg nreg_10 (
    .Clear(nreg_9_out_clear), .Button(nreg_9_out_button), .Input(nreg_9_out_input),
    .Out_Clear(nreg_10_out_clear), .Out_Button(nreg_10_out_button), .Out_Input(nreg_10_out_input));  // open: Enabled, Output
  nReg nreg_11 (
    .Clear(nreg_10_out_clear), .Button(nreg_10_out_button), .Input(nreg_10_out_input),
    .Out_Clear(nreg_11_out_clear), .Out_Button(nreg_11_out_button), .Out_Input(nreg_11_out_input));  // open: Enabled, Output
  nReg nreg_12 (
    .Clear(nreg_11_out_clear), .Button(nreg_11_out_button), .Input(nreg_11_out_input),
    .Out_Clear(nreg_12_out_clear), .Out_Button(nreg_12_out_button), .Out_Input(nreg_12_out_input));  // open: Enabled, Output
  nReg nreg_13 (
    .Clear(nreg_12_out_clear), .Button(nreg_12_out_button), .Input(nreg_12_out_input),
    .Out_Clear(nreg_13_out_clear), .Out_Button(nreg_13_out_button), .Out_Input(nreg_13_out_input));  // open: Enabled, Output
  nReg nreg_14 (
    .Clear(nreg_13_out_clear), .Button(nreg_13_out_button), .Input(nreg_13_out_input),
    .Out_Clear(nreg_14_out_clear), .Out_Button(nreg_14_out_button), .Out_Input(nreg_14_out_input));  // open: Enabled, Output
  nReg nreg_15 (
    .Clear(nreg_14_out_clear), .Button(nreg_14_out_button), .Input(nreg_14_out_input),
    .Out_Clear(nreg_15_out_clear), .Out_Button(nreg_15_out_button), .Out_Input(nreg_15_out_input));  // open: Enabled, Output
  nReg nreg_16 (
    .Clear(nreg_15_out_clear), .Button(nreg_15_out_button), .Input(nreg_15_out_input),
    .Out_Clear(nreg_16_out_clear), .Out_Button(nreg_16_out_button), .Out_Input(nreg_16_out_input));  // open: Enabled, Output
  nReg nreg_17 (
    .Clear(nreg_16_out_clear), .Button(nreg_16_out_button), .Input(nreg_16_out_input),
    .Out_Clear(nreg_17_out_clear), .Out_Button(nreg_17_out_button), .Out_Input(nreg_17_out_input));  // open: Enabled, Output
  nReg nreg_18 (
    .Clear(nreg_17_out_clear), .Button(nreg_17_out_button), .Input(nreg_17_out_input),
    .Out_Clear(nreg_18_out_clear), .Out_Button(nreg_18_out_button), .Out_Input(nreg_18_out_input));  // open: Enabled, Output
  nReg nreg_19 (
    .Clear(nreg_18_out_clear), .Button(nreg_18_out_button), .Input(nreg_18_out_input),
    .Out_Clear(nreg_19_out_clear), .Out_Button(nreg_19_out_button), .Out_Input(nreg_19_out_input));  // open: Enabled, Output
  nReg nreg_20 (
    .Clear(nreg_19_out_clear), .Button(nreg_19_out_button), .Input(nreg_19_out_input),
    .Out_Clear(nreg_20_out_clear), .Out_Button(nreg_20_out_button), .Out_Input(nreg_20_out_input));  // open: Enabled, Output
  nReg nreg_21 (
    .Clear(nreg_20_out_clear), .Button(nreg_20_out_button), .Input(nreg_20_out_input),
    .Out_Clear(nreg_21_out_clear), .Out_Button(nreg_21_out_button), .Out_Input(nreg_21_out_input));  // open: Enabled, Output
  nReg nreg_22 (
    .Clear(nreg_21_out_clear), .Button(nreg_21_out_button), .Input(nreg_21_out_input),
    .Out_Clear(nreg_22_out_clear), .Out_Button(nreg_22_out_button), .Out_Input(nreg_22_out_input));  // open: Enabled, Output
  nReg nreg_23 (
    .Clear(nreg_22_out_clear), .Button(nreg_22_out_button), .Input(nreg_22_out_input),
    .Out_Clear(nreg_23_out_clear), .Out_Button(nreg_23_out_button), .Out_Input(nreg_23_out_input));  // open: Enabled, Output
  nReg nreg_24 (
    .Clear(nreg_23_out_clear), .Button(nreg_23_out_button), .Input(nreg_23_out_input),
    .Out_Clear(nreg_24_out_clear), .Out_Button(nreg_24_out_button), .Out_Input(nreg_24_out_input));  // open: Enabled, Output
  nReg nreg_25 (
    .Clear(nreg_24_out_clear), .Button(nreg_24_out_button), .Input(nreg_24_out_input),
    .Out_Clear(nreg_25_out_clear), .Out_Button(nreg_25_out_button), .Out_Input(nreg_25_out_input));  // open: Enabled, Output
  nReg nreg_26 (
    .Clear(nreg_25_out_clear), .Button(nreg_25_out_button), .Input(nreg_25_out_input),
    .Out_Clear(nreg_26_out_clear), .Out_Button(nreg_26_out_button), .Out_Input(nreg_26_out_input));  // open: Enabled, Output
  nReg nreg_27 (
    .Clear(nreg_26_out_clear), .Button(nreg_26_out_button), .Input(nreg_26_out_input),
    .Out_Clear(nreg_27_out_clear), .Out_Button(nreg_27_out_button), .Out_Input(nreg_27_out_input));  // open: Enabled, Output
  nReg nreg_28 (
    .Clear(nreg_27_out_clear), .Button(nreg_27_out_button), .Input(nreg_27_out_input),
    .Out_Clear(nreg_28_out_clear), .Out_Button(nreg_28_out_button), .Out_Input(nreg_28_out_input));  // open: Enabled, Output
  nReg nreg_29 (
    .Clear(nreg_28_out_clear), .Button(nreg_28_out_button), .Input(nreg_28_out_input),
    .Out_Clear(nreg_29_out_clear), .Out_Button(nreg_29_out_button), .Out_Input(nreg_29_out_input));  // open: Enabled, Output
  nReg nreg_30 (
    .Clear(nreg_29_out_clear), .Button(nreg_29_out_button), .Input(nreg_29_out_input),
    .Out_Clear(nreg_30_out_clear), .Out_Button(nreg_30_out_button), .Out_Input(nreg_30_out_input));  // open: Enabled, Output
  nReg nreg_31 (
    .Clear(nreg_30_out_clear), .Button(nreg_30_out_button), .Input(nreg_30_out_input),
    .Out_Clear(nreg_31_out_clear), .Out_Button(nreg_31_out_button), .Out_Input(nreg_31_out_input));  // open: Enabled, Output
  nReg nreg_32 (
    .Clear(nreg_31_out_clear), .Button(nreg_31_out_button), .Input(nreg_31_out_input));  // open: Enabled, Output, Out_Clear, Out_Button, Out_Input
  not not_1 (C, Clock);
  BitFinder #(.width(32)) bitfinder_1 (.in(X_Location_1), .index(bitfinder_1_index), .found(bitfinder_1_found));
  BitFinder #(.width(32)) bitfinder_2 (.in(X_Location_2), .index(bitfinder_2_index), .found(bitfinder_2_found));
  not not_2 (not_2_out, Move);
  assign Y = not_2_out ? Y_Location : 32'bz;  // Controlled_Buffer controlled_buffer_1
  assign Y = Move ? {32{1'b0}} : 32'bz;  // Controlled_Buffer controlled_buffer_2
  dReg dreg_1 (
    .Enabled(decoder_1_out0), .Out_Draw({Draw, dreg_1_out_draw}), .Out_Clear({Reset, dreg_1_out_clear}),
    .Button({and_1_out, undriven_2}), .Input_Overwrite(demultiplexer_1_out0), .Input(Y),
    .Overwrite({Loading, undriven_65}), .Out_Input(dreg_1_out_input), .Output(Out_1), .overCMD(decoder_3_out0));
  dReg dreg_2 (
    .Enabled(decoder_1_out1), .Out_Draw({dreg_1_out_draw, dreg_2_out_draw}),
    .Out_Clear({dreg_1_out_clear, dreg_2_out_clear}), .Button({undriven_2, undriven_3}),
    .Input_Overwrite(demultiplexer_1_out1), .Input(dreg_1_out_input), .Overwrite({undriven_65, undriven_66}),
    .Out_Input(dreg_2_out_input), .Output(Out_2), .overCMD(decoder_3_out1));
  dReg dreg_3 (
    .Enabled(decoder_1_out2), .Out_Draw({dreg_2_out_draw, dreg_3_out_draw}),
    .Out_Clear({dreg_2_out_clear, dreg_3_out_clear}), .Button({undriven_3, undriven_4}),
    .Input_Overwrite(demultiplexer_1_out2), .Input(dreg_2_out_input), .Overwrite({undriven_66, undriven_67}),
    .Out_Input(dreg_3_out_input), .Output(Out_3), .overCMD(decoder_3_out2));
  dReg dreg_4 (
    .Enabled(decoder_1_out3), .Out_Draw({dreg_3_out_draw, dreg_4_out_draw}),
    .Out_Clear({dreg_3_out_clear, dreg_4_out_clear}), .Button({undriven_4, undriven_5}),
    .Input_Overwrite(demultiplexer_1_out3), .Input(dreg_3_out_input), .Overwrite({undriven_67, undriven_68}),
    .Out_Input(dreg_4_out_input), .Output(Out_4), .overCMD(decoder_3_out3));
  dReg dreg_5 (
    .Enabled(decoder_1_out4), .Out_Draw({dreg_4_out_draw, dreg_5_out_draw}),
    .Out_Clear({dreg_4_out_clear, dreg_5_out_clear}), .Button({undriven_5, undriven_6}),
    .Input_Overwrite(demultiplexer_1_out4), .Input(dreg_4_out_input), .Overwrite({undriven_68, undriven_69}),
    .Out_Input(dreg_5_out_input), .Output(Out_5), .overCMD(decoder_3_out4));
  dReg dreg_6 (
    .Enabled(decoder_1_out5), .Out_Draw({dreg_5_out_draw, dreg_6_out_draw}),
    .Out_Clear({dreg_5_out_clear, dreg_6_out_clear}), .Button({undriven_6, undriven_7}),
    .Input_Overwrite(demultiplexer_1_out5), .Input(dreg_5_out_input), .Overwrite({undriven_69, undriven_70}),
    .Out_Input(dreg_6_out_input), .Output(Out_6), .overCMD(decoder_3_out5));
  dReg dreg_7 (
    .Enabled(decoder_1_out6), .Out_Draw({dreg_6_out_draw, dreg_7_out_draw}),
    .Out_Clear({dreg_6_out_clear, dreg_7_out_clear}), .Button({undriven_7, undriven_8}),
    .Input_Overwrite(demultiplexer_1_out6), .Input(dreg_6_out_input), .Overwrite({undriven_70, undriven_71}),
    .Out_Input(dreg_7_out_input), .Output(Out_7), .overCMD(decoder_3_out6));
  dReg dreg_8 (
    .Enabled(decoder_1_out7), .Out_Draw({dreg_7_out_draw, dreg_8_out_draw}),
    .Out_Clear({dreg_7_out_clear, dreg_8_out_clear}), .Button({undriven_8, undriven_9}),
    .Input_Overwrite(demultiplexer_1_out7), .Input(dreg_7_out_input), .Overwrite({undriven_71, undriven_72}),
    .Out_Input(dreg_8_out_input), .Output(Out_8), .overCMD(decoder_3_out7));
  dReg dreg_9 (
    .Enabled(decoder_1_out8), .Out_Draw({dreg_8_out_draw, dreg_9_out_draw}),
    .Out_Clear({dreg_8_out_clear, dreg_9_out_clear}), .Button({undriven_9, undriven_10}),
    .Input_Overwrite(demultiplexer_1_out8), .Input(dreg_8_out_input), .Overwrite({undriven_72, undriven_73}),
    .Out_Input(dreg_9_out_input), .Output(Out_9), .overCMD(decoder_3_out8));
  dReg dreg_10 (
    .Enabled(decoder_1_out9), .Out_Draw({dreg_9_out_draw, dreg_10_out_draw}),
    .Out_Clear({dreg_9_out_clear, dreg_10_out_clear}), .Button({undriven_10, undriven_11}),
    .Input_Overwrite(demultiplexer_1_out9), .Input(dreg_9_out_input), .Overwrite({undriven_73, undriven_74}),
    .Out_Input(dreg_10_out_input), .Output(Out_10), .overCMD(decoder_3_out9));
  dReg dreg_11 (
    .Enabled(decoder_1_out10), .Out_Draw({dreg_10_out_draw, dreg_11_out_draw}),
    .Out_Clear({dreg_10_out_clear, dreg_11_out_clear}), .Button({undriven_11, undriven_12}),
    .Input_Overwrite(demultiplexer_1_out10), .Input(dreg_10_out_input),
    .Overwrite({undriven_74, undriven_75}), .Out_Input(dreg_11_out_input), .Output(Out_11),
    .overCMD(decoder_3_out10));
  dReg dreg_12 (
    .Enabled(decoder_1_out11), .Out_Draw({dreg_11_out_draw, dreg_12_out_draw}),
    .Out_Clear({dreg_11_out_clear, dreg_12_out_clear}), .Button({undriven_12, undriven_13}),
    .Input_Overwrite(demultiplexer_1_out11), .Input(dreg_11_out_input),
    .Overwrite({undriven_75, undriven_76}), .Out_Input(dreg_12_out_input), .Output(Out_12),
    .overCMD(decoder_3_out11));
  dReg dreg_13 (
    .Enabled(decoder_1_out12), .Out_Draw({dreg_12_out_draw, dreg_13_out_draw}),
    .Out_Clear({dreg_12_out_clear, dreg_13_out_clear}), .Button({undriven_13, undriven_14}),
    .Input_Overwrite(demultiplexer_1_out12), .Input(dreg_12_out_input),
    .Overwrite({undriven_76, undriven_77}), .Out_Input(dreg_13_out_input), .Output(Out_13),
    .overCMD(decoder_3_out12));
  dReg dreg_14 (
    .Enabled(decoder_1_out13), .Out_Draw({dreg_13_out_draw, dreg_14_out_draw}),
    .Out_Clear({dreg_13_out_clear, dreg_14_out_clear}), .Button({undriven_14, undriven_15}),
    .Input_Overwrite(demultiplexer_1_out13), .Input(dreg_13_out_input),
    .Overwrite({undriven_77, undriven_78}), .Out_Input(dreg_14_out_input), .Output(Out_14),
    .overCMD(decoder_3_out13));
  dReg dreg_15 (
    .Enabled(decoder_1_out14), .Out_Draw({dreg_14_out_draw, dreg_15_out_draw}),
    .Out_Clear({dreg_14_out_clear, dreg_15_out_clear}), .Button({undriven_15, undriven_16}),
    .Input_Overwrite(demultiplexer_1_out14), .Input(dreg_14_out_input),
    .Overwrite({undriven_78, undriven_79}), .Out_Input(dreg_15_out_input), .Output(Out_15),
    .overCMD(decoder_3_out14));
  dReg dreg_16 (
    .Enabled(decoder_1_out15), .Out_Draw({dreg_15_out_draw, dreg_16_out_draw}),
    .Out_Clear({dreg_15_out_clear, dreg_16_out_clear}), .Button({undriven_16, undriven_17}),
    .Input_Overwrite(demultiplexer_1_out15), .Input(dreg_15_out_input),
    .Overwrite({undriven_79, undriven_80}), .Out_Input(dreg_16_out_input), .Output(Out_16),
    .overCMD(decoder_3_out15));
  dReg dreg_17 (
    .Enabled(decoder_1_out16), .Out_Draw({dreg_16_out_draw, dreg_17_out_draw}),
    .Out_Clear({dreg_16_out_clear, dreg_17_out_clear}), .Button({undriven_17, undriven_18}),
    .Input_Overwrite(demultiplexer_1_out16), .Input(dreg_16_out_input),
    .Overwrite({undriven_80, undriven_81}), .Out_Input(dreg_17_out_input), .Output(Out_17),
    .overCMD(decoder_3_out16));
  dReg dreg_18 (
    .Enabled(decoder_1_out17), .Out_Draw({dreg_17_out_draw, dreg_18_out_draw}),
    .Out_Clear({dreg_17_out_clear, dreg_18_out_clear}), .Button({undriven_18, undriven_19}),
    .Input_Overwrite(demultiplexer_1_out17), .Input(dreg_17_out_input),
    .Overwrite({undriven_81, undriven_82}), .Out_Input(dreg_18_out_input), .Output(Out_18),
    .overCMD(decoder_3_out17));
  dReg dreg_19 (
    .Enabled(decoder_1_out18), .Out_Draw({dreg_18_out_draw, dreg_19_out_draw}),
    .Out_Clear({dreg_18_out_clear, dreg_19_out_clear}), .Button({undriven_19, undriven_20}),
    .Input_Overwrite(demultiplexer_1_out18), .Input(dreg_18_out_input),
    .Overwrite({undriven_82, undriven_83}), .Out_Input(dreg_19_out_input), .Output(Out_19),
    .overCMD(decoder_3_out18));
  dReg dreg_20 (
    .Enabled(decoder_1_out19), .Out_Draw({dreg_19_out_draw, dreg_20_out_draw}),
    .Out_Clear({dreg_19_out_clear, dreg_20_out_clear}), .Button({undriven_20, undriven_21}),
    .Input_Overwrite(demultiplexer_1_out19), .Input(dreg_19_out_input),
    .Overwrite({undriven_83, undriven_84}), .Out_Input(dreg_20_out_input), .Output(Out_20),
    .overCMD(decoder_3_out19));
  dReg dreg_21 (
    .Enabled(decoder_1_out20), .Out_Draw({dreg_20_out_draw, dreg_21_out_draw}),
    .Out_Clear({dreg_20_out_clear, dreg_21_out_clear}), .Button({undriven_21, undriven_22}),
    .Input_Overwrite(demultiplexer_1_out20), .Input(dreg_20_out_input),
    .Overwrite({undriven_84, undriven_85}), .Out_Input(dreg_21_out_input), .Output(Out_21),
    .overCMD(decoder_3_out20));
  dReg dreg_22 (
    .Enabled(decoder_1_out21), .Out_Draw({dreg_21_out_draw, dreg_22_out_draw}),
    .Out_Clear({dreg_21_out_clear, dreg_22_out_clear}), .Button({undriven_22, undriven_23}),
    .Input_Overwrite(demultiplexer_1_out21), .Input(dreg_21_out_input),
    .Overwrite({undriven_85, undriven_86}), .Out_Input(dreg_22_out_input), .Output(Out_22),
    .overCMD(decoder_3_out21));
  dReg dreg_23 (
    .Enabled(decoder_1_out22), .Out_Draw({dreg_22_out_draw, dreg_23_out_draw}),
    .Out_Clear({dreg_22_out_clear, dreg_23_out_clear}), .Button({undriven_23, undriven_24}),
    .Input_Overwrite(demultiplexer_1_out22), .Input(dreg_22_out_input),
    .Overwrite({undriven_86, undriven_87}), .Out_Input(dreg_23_out_input), .Output(Out_23),
    .overCMD(decoder_3_out22));
  dReg dreg_24 (
    .Enabled(decoder_1_out23), .Out_Draw({dreg_23_out_draw, dreg_24_out_draw}),
    .Out_Clear({dreg_23_out_clear, dreg_24_out_clear}), .Button({undriven_24, undriven_25}),
    .Input_Overwrite(demultiplexer_1_out23), .Input(dreg_23_out_input),
    .Overwrite({undriven_87, undriven_88}), .Out_Input(dreg_24_out_input), .Output(Out_24),
    .overCMD(decoder_3_out23));
  dReg dreg_25 (
    .Enabled(decoder_1_out24), .Out_Draw({dreg_24_out_draw, dreg_25_out_draw}),
    .Out_Clear({dreg_24_out_clear, dreg_25_out_clear}), .Button({undriven_25, undriven_26}),
    .Input_Overwrite(demultiplexer_1_out24), .Input(dreg_24_out_input),
    .Overwrite({undriven_88, undriven_89}), .Out_Input(dreg_25_out_input), .Output(Out_25),
    .overCMD(decoder_3_out24));
  dReg dreg_26 (
    .Enabled(decoder_1_out25), .Out_Draw({dreg_25_out_draw, dreg_26_out_draw}),
    .Out_Clear({dreg_25_out_clear, dreg_26_out_clear}), .Button({undriven_26, undriven_27}),
    .Input_Overwrite(demultiplexer_1_out25), .Input(dreg_25_out_input),
    .Overwrite({undriven_89, undriven_90}), .Out_Input(dreg_26_out_input), .Output(Out_26),
    .overCMD(decoder_3_out25));
  dReg dreg_27 (
    .Enabled(decoder_1_out26), .Out_Draw({dreg_26_out_draw, dreg_27_out_draw}),
    .Out_Clear({dreg_26_out_clear, dreg_27_out_clear}), .Button({undriven_27, undriven_28}),
    .Input_Overwrite(demultiplexer_1_out26), .Input(dreg_26_out_input),
    .Overwrite({undriven_90, undriven_91}), .Out_Input(dreg_27_out_input), .Output(Out_27),
    .overCMD(decoder_3_out26));
  dReg dreg_28 (
    .Enabled(decoder_1_out27), .Out_Draw({dreg_27_out_draw, dreg_28_out_draw}),
    .Out_Clear({dreg_27_out_clear, dreg_28_out_clear}), .Button({undriven_28, undriven_29}),
    .Input_Overwrite(demultiplexer_1_out27), .Input(dreg_27_out_input),
    .Overwrite({undriven_91, undriven_92}), .Out_Input(dreg_28_out_input), .Output(Out_28),
    .overCMD(decoder_3_out27));
  dReg dreg_29 (
    .Enabled(decoder_1_out28), .Out_Draw({dreg_28_out_draw, dreg_29_out_draw}),
    .Out_Clear({dreg_28_out_clear, dreg_29_out_clear}), .Button({undriven_29, undriven_30}),
    .Input_Overwrite(demultiplexer_1_out28), .Input(dreg_28_out_input),
    .Overwrite({undriven_92, undriven_93}), .Out_Input(dreg_29_out_input), .Output(Out_29),
    .overCMD(decoder_3_out28));
  dReg dreg_30 (
    .Enabled(decoder_1_out29), .Out_Draw({dreg_29_out_draw, dreg_30_out_draw}),
    .Out_Clear({dreg_29_out_clear, dreg_30_out_clear}), .Button({undriven_30, undriven_31}),
    .Input_Overwrite(demultiplexer_1_out29), .Input(dreg_29_out_input),
    .Overwrite({undriven_93, undriven_94}), .Out_Input(dreg_30_out_input), .Output(Out_30),
    .overCMD(decoder_3_out29));
  dReg dreg_31 (
    .Enabled(decoder_1_out30), .Out_Draw({dreg_30_out_draw, dreg_31_out_draw}),
    .Out_Clear({dreg_30_out_clear, dreg_31_out_clear}), .Button({undriven_31, undriven_32}),
    .Input_Overwrite(demultiplexer_1_out30), .Input(dreg_30_out_input),
    .Overwrite({undriven_94, undriven_95}), .Out_Input(dreg_31_out_input), .Output(Out_31),
    .overCMD(decoder_3_out30));
  dReg dreg_32 (
    .Enabled(decoder_1_out31), .Out_Draw({dreg_31_out_draw, dreg_32_out_draw}),
    .Out_Clear({dreg_31_out_clear, dreg_32_out_clear}), .Button({undriven_32, undriven_33}),
    .Input_Overwrite(demultiplexer_1_out31), .Input(dreg_31_out_input),
    .Overwrite({undriven_95, undriven_96}), .Out_Input(dreg_32_out_input), .Output(Out_32),
    .overCMD(decoder_3_out31));
  Decoder #(.select(5)) decoder_1 (
    .out0(decoder_1_out0), .out1(decoder_1_out1), .out2(decoder_1_out2), .out3(decoder_1_out3),
    .out4(decoder_1_out4), .out5(decoder_1_out5), .out6(decoder_1_out6), .out7(decoder_1_out7),
    .out8(decoder_1_out8), .out9(decoder_1_out9), .out10(decoder_1_out10), .out11(decoder_1_out11),
    .out12(decoder_1_out12), .out13(decoder_1_out13), .out14(decoder_1_out14), .out15(decoder_1_out15),
    .out16(decoder_1_out16), .out17(decoder_1_out17), .out18(decoder_1_out18), .out19(decoder_1_out19),
    .out20(decoder_1_out20), .out21(decoder_1_out21), .out22(decoder_1_out22), .out23(decoder_1_out23),
    .out24(decoder_1_out24), .out25(decoder_1_out25), .out26(decoder_1_out26), .out27(decoder_1_out27),
    .out28(decoder_1_out28), .out29(decoder_1_out29), .out30(decoder_1_out30), .out31(decoder_1_out31),
    .sel(bitfinder_1_index), .en(bitfinder_1_found));
  dReg dreg_33 (
    .Enabled(decoder_2_out0), .Out_Draw({dreg_32_out_draw, dreg_33_out_draw}),
    .Out_Clear({dreg_32_out_clear, dreg_33_out_clear}), .Button({undriven_33, undriven_34}),
    .Input_Overwrite(demultiplexer_2_out0), .Input(dreg_32_out_input),
    .Overwrite({undriven_96, undriven_97}), .Out_Input(dreg_33_out_input), .Output(Out_33),
    .overCMD(decoder_4_out0));
  Decoder #(.select(5)) decoder_2 (
    .out0(decoder_2_out0), .out1(decoder_2_out1), .out2(decoder_2_out2), .out3(decoder_2_out3),
    .out4(decoder_2_out4), .out5(decoder_2_out5), .out6(decoder_2_out6), .out7(decoder_2_out7),
    .out8(decoder_2_out8), .out9(decoder_2_out9), .out10(decoder_2_out10), .out11(decoder_2_out11),
    .out12(decoder_2_out12), .out13(decoder_2_out13), .out14(decoder_2_out14), .out15(decoder_2_out15),
    .out16(decoder_2_out16), .out17(decoder_2_out17), .out18(decoder_2_out18), .out19(decoder_2_out19),
    .out20(decoder_2_out20), .out21(decoder_2_out21), .out22(decoder_2_out22), .out23(decoder_2_out23),
    .out24(decoder_2_out24), .out25(decoder_2_out25), .out26(decoder_2_out26), .out27(decoder_2_out27),
    .out28(decoder_2_out28), .out29(decoder_2_out29), .out30(decoder_2_out30), .out31(decoder_2_out31),
    .sel(bitfinder_2_index), .en(bitfinder_2_found));
  dReg dreg_34 (
    .Enabled(decoder_2_out1), .Out_Draw({dreg_33_out_draw, dreg_34_out_draw}),
    .Out_Clear({dreg_33_out_clear, dreg_34_out_clear}), .Button({undriven_34, undriven_35}),
    .Input_Overwrite(demultiplexer_2_out1), .Input(dreg_33_out_input),
    .Overwrite({undriven_97, undriven_98}), .Out_Input(dreg_34_out_input), .Output(Out_34),
    .overCMD(decoder_4_out1));
  dReg dreg_35 (
    .Enabled(decoder_2_out2), .Out_Draw({dreg_34_out_draw, dreg_35_out_draw}),
    .Out_Clear({dreg_34_out_clear, dreg_35_out_clear}), .Button({undriven_35, undriven_36}),
    .Input_Overwrite(demultiplexer_2_out2), .Input(dreg_34_out_input),
    .Overwrite({undriven_98, undriven_99}), .Out_Input(dreg_35_out_input), .Output(Out_35),
    .overCMD(decoder_4_out2));
  dReg dreg_36 (
    .Enabled(decoder_2_out3), .Out_Draw({dreg_35_out_draw, dreg_36_out_draw}),
    .Out_Clear({dreg_35_out_clear, dreg_36_out_clear}), .Button({undriven_36, undriven_37}),
    .Input_Overwrite(demultiplexer_2_out3), .Input(dreg_35_out_input),
    .Overwrite({undriven_99, undriven_100}), .Out_Input(dreg_36_out_input), .Output(Out_36),
    .overCMD(decoder_4_out3));
  dReg dreg_37 (
    .Enabled(decoder_2_out4), .Out_Draw({dreg_36_out_draw, dreg_37_out_draw}),
    .Out_Clear({dreg_36_out_clear, dreg_37_out_clear}), .Button({undriven_37, undriven_38}),
    .Input_Overwrite(demultiplexer_2_out4), .Input(dreg_36_out_input),
    .Overwrite({undriven_100, undriven_101}), .Out_Input(dreg_37_out_input), .Output(Out_37),
    .overCMD(decoder_4_out4));
  dReg dreg_38 (
    .Enabled(decoder_2_out5), .Out_Draw({dreg_37_out_draw, dreg_38_out_draw}),
    .Out_Clear({dreg_37_out_clear, dreg_38_out_clear}), .Button({undriven_38, undriven_39}),
    .Input_Overwrite(demultiplexer_2_out5), .Input(dreg_37_out_input),
    .Overwrite({undriven_101, undriven_102}), .Out_Input(dreg_38_out_input), .Output(Out_38),
    .overCMD(decoder_4_out5));
  dReg dreg_39 (
    .Enabled(decoder_2_out6), .Out_Draw({dreg_38_out_draw, dreg_39_out_draw}),
    .Out_Clear({dreg_38_out_clear, dreg_39_out_clear}), .Button({undriven_39, undriven_40}),
    .Input_Overwrite(demultiplexer_2_out6), .Input(dreg_38_out_input),
    .Overwrite({undriven_102, undriven_103}), .Out_Input(dreg_39_out_input), .Output(Out_39),
    .overCMD(decoder_4_out6));
  dReg dreg_40 (
    .Enabled(decoder_2_out7), .Out_Draw({dreg_39_out_draw, dreg_40_out_draw}),
    .Out_Clear({dreg_39_out_clear, dreg_40_out_clear}), .Button({undriven_40, undriven_41}),
    .Input_Overwrite(demultiplexer_2_out7), .Input(dreg_39_out_input),
    .Overwrite({undriven_103, undriven_104}), .Out_Input(dreg_40_out_input), .Output(Out_40),
    .overCMD(decoder_4_out7));
  dReg dreg_41 (
    .Enabled(decoder_2_out8), .Out_Draw({dreg_40_out_draw, dreg_41_out_draw}),
    .Out_Clear({dreg_40_out_clear, dreg_41_out_clear}), .Button({undriven_41, undriven_42}),
    .Input_Overwrite(demultiplexer_2_out8), .Input(dreg_40_out_input),
    .Overwrite({undriven_104, undriven_105}), .Out_Input(dreg_41_out_input), .Output(Out_41),
    .overCMD(decoder_4_out8));
  dReg dreg_42 (
    .Enabled(decoder_2_out9), .Out_Draw({dreg_41_out_draw, dreg_42_out_draw}),
    .Out_Clear({dreg_41_out_clear, dreg_42_out_clear}), .Button({undriven_42, undriven_43}),
    .Input_Overwrite(demultiplexer_2_out9), .Input(dreg_41_out_input),
    .Overwrite({undriven_105, undriven_106}), .Out_Input(dreg_42_out_input), .Output(Out_42),
    .overCMD(decoder_4_out9));
  dReg dreg_43 (
    .Enabled(decoder_2_out10), .Out_Draw({dreg_42_out_draw, dreg_43_out_draw}),
    .Out_Clear({dreg_42_out_clear, dreg_43_out_clear}), .Button({undriven_43, undriven_44}),
    .Input_Overwrite(demultiplexer_2_out10), .Input(dreg_42_out_input),
    .Overwrite({undriven_106, undriven_107}), .Out_Input(dreg_43_out_input), .Output(Out_43),
    .overCMD(decoder_4_out10));
  dReg dreg_44 (
    .Enabled(decoder_2_out11), .Out_Draw({dreg_43_out_draw, dreg_44_out_draw}),
    .Out_Clear({dreg_43_out_clear, dreg_44_out_clear}), .Button({undriven_44, undriven_45}),
    .Input_Overwrite(demultiplexer_2_out11), .Input(dreg_43_out_input),
    .Overwrite({undriven_107, undriven_108}), .Out_Input(dreg_44_out_input), .Output(Out_44),
    .overCMD(decoder_4_out11));
  dReg dreg_45 (
    .Enabled(decoder_2_out12), .Out_Draw({dreg_44_out_draw, dreg_45_out_draw}),
    .Out_Clear({dreg_44_out_clear, dreg_45_out_clear}), .Button({undriven_45, undriven_46}),
    .Input_Overwrite(demultiplexer_2_out12), .Input(dreg_44_out_input),
    .Overwrite({undriven_108, undriven_109}), .Out_Input(dreg_45_out_input), .Output(Out_45),
    .overCMD(decoder_4_out12));
  dReg dreg_46 (
    .Enabled(decoder_2_out13), .Out_Draw({dreg_45_out_draw, dreg_46_out_draw}),
    .Out_Clear({dreg_45_out_clear, dreg_46_out_clear}), .Button({undriven_46, undriven_47}),
    .Input_Overwrite(demultiplexer_2_out13), .Input(dreg_45_out_input),
    .Overwrite({undriven_109, undriven_110}), .Out_Input(dreg_46_out_input), .Output(Out_46),
    .overCMD(decoder_4_out13));
  dReg dreg_47 (
    .Enabled(decoder_2_out14), .Out_Draw({dreg_46_out_draw, dreg_47_out_draw}),
    .Out_Clear({dreg_46_out_clear, dreg_47_out_clear}), .Button({undriven_47, undriven_48}),
    .Input_Overwrite(demultiplexer_2_out14), .Input(dreg_46_out_input),
    .Overwrite({undriven_110, undriven_111}), .Out_Input(dreg_47_out_input), .Output(Out_47),
    .overCMD(decoder_4_out14));
  dReg dreg_48 (
    .Enabled(decoder_2_out15), .Out_Draw({dreg_47_out_draw, dreg_48_out_draw}),
    .Out_Clear({dreg_47_out_clear, dreg_48_out_clear}), .Button({undriven_48, undriven_49}),
    .Input_Overwrite(demultiplexer_2_out15), .Input(dreg_47_out_input),
    .Overwrite({undriven_111, undriven_112}), .Out_Input(dreg_48_out_input), .Output(Out_48),
    .overCMD(decoder_4_out15));
  dReg dreg_49 (
    .Enabled(decoder_2_out16), .Out_Draw({dreg_48_out_draw, dreg_49_out_draw}),
    .Out_Clear({dreg_48_out_clear, dreg_49_out_clear}), .Button({undriven_49, undriven_50}),
    .Input_Overwrite(demultiplexer_2_out16), .Input(dreg_48_out_input),
    .Overwrite({undriven_112, undriven_113}), .Out_Input(dreg_49_out_input), .Output(Out_49),
    .overCMD(decoder_4_out16));
  dReg dreg_50 (
    .Enabled(decoder_2_out17), .Out_Draw({dreg_49_out_draw, dreg_50_out_draw}),
    .Out_Clear({dreg_49_out_clear, dreg_50_out_clear}), .Button({undriven_50, undriven_51}),
    .Input_Overwrite(demultiplexer_2_out17), .Input(dreg_49_out_input),
    .Overwrite({undriven_113, undriven_114}), .Out_Input(dreg_50_out_input), .Output(Out_50),
    .overCMD(decoder_4_out17));
  dReg dreg_51 (
    .Enabled(decoder_2_out18), .Out_Draw({dreg_50_out_draw, dreg_51_out_draw}),
    .Out_Clear({dreg_50_out_clear, dreg_51_out_clear}), .Button({undriven_51, undriven_52}),
    .Input_Overwrite(demultiplexer_2_out18), .Input(dreg_50_out_input),
    .Overwrite({undriven_114, undriven_115}), .Out_Input(dreg_51_out_input), .Output(Out_51),
    .overCMD(decoder_4_out18));
  dReg dreg_52 (
    .Enabled(decoder_2_out19), .Out_Draw({dreg_51_out_draw, dreg_52_out_draw}),
    .Out_Clear({dreg_51_out_clear, dreg_52_out_clear}), .Button({undriven_52, undriven_53}),
    .Input_Overwrite(demultiplexer_2_out19), .Input(dreg_51_out_input),
    .Overwrite({undriven_115, undriven_116}), .Out_Input(dreg_52_out_input), .Output(Out_52),
    .overCMD(decoder_4_out19));
  dReg dreg_53 (
    .Enabled(decoder_2_out20), .Out_Draw({dreg_52_out_draw, dreg_53_out_draw}),
    .Out_Clear({dreg_52_out_clear, dreg_53_out_clear}), .Button({undriven_53, undriven_54}),
    .Input_Overwrite(demultiplexer_2_out20), .Input(dreg_52_out_input),
    .Overwrite({undriven_116, undriven_117}), .Out_Input(dreg_53_out_input), .Output(Out_53),
    .overCMD(decoder_4_out20));
  dReg dreg_54 (
    .Enabled(decoder_2_out21), .Out_Draw({dreg_53_out_draw, dreg_54_out_draw}),
    .Out_Clear({dreg_53_out_clear, dreg_54_out_clear}), .Button({undriven_54, undriven_55}),
    .Input_Overwrite(demultiplexer_2_out21), .Input(dreg_53_out_input),
    .Overwrite({undriven_117, undriven_118}), .Out_Input(dreg_54_out_input), .Output(Out_54),
    .overCMD(decoder_4_out21));
  dReg dreg_55 (
    .Enabled(decoder_2_out22), .Out_Draw({dreg_54_out_draw, dreg_55_out_draw}),
    .Out_Clear({dreg_54_out_clear, dreg_55_out_clear}), .Button({undriven_55, undriven_56}),
    .Input_Overwrite(demultiplexer_2_out22), .Input(dreg_54_out_input),
    .Overwrite({undriven_118, undriven_119}), .Out_Input(dreg_55_out_input), .Output(Out_55),
    .overCMD(decoder_4_out22));
  dReg dreg_56 (
    .Enabled(decoder_2_out23), .Out_Draw({dreg_55_out_draw, dreg_56_out_draw}),
    .Out_Clear({dreg_55_out_clear, dreg_56_out_clear}), .Button({undriven_56, undriven_57}),
    .Input_Overwrite(demultiplexer_2_out23), .Input(dreg_55_out_input),
    .Overwrite({undriven_119, undriven_120}), .Out_Input(dreg_56_out_input), .Output(Out_56),
    .overCMD(decoder_4_out23));
  dReg dreg_57 (
    .Enabled(decoder_2_out24), .Out_Draw({dreg_56_out_draw, dreg_57_out_draw}),
    .Out_Clear({dreg_56_out_clear, dreg_57_out_clear}), .Button({undriven_57, undriven_58}),
    .Input_Overwrite(demultiplexer_2_out24), .Input(dreg_56_out_input),
    .Overwrite({undriven_120, undriven_121}), .Out_Input(dreg_57_out_input), .Output(Out_57),
    .overCMD(decoder_4_out24));
  dReg dreg_58 (
    .Enabled(decoder_2_out25), .Out_Draw({dreg_57_out_draw, dreg_58_out_draw}),
    .Out_Clear({dreg_57_out_clear, dreg_58_out_clear}), .Button({undriven_58, undriven_59}),
    .Input_Overwrite(demultiplexer_2_out25), .Input(dreg_57_out_input),
    .Overwrite({undriven_121, undriven_122}), .Out_Input(dreg_58_out_input), .Output(Out_58),
    .overCMD(decoder_4_out25));
  dReg dreg_59 (
    .Enabled(decoder_2_out26), .Out_Draw({dreg_58_out_draw, dreg_59_out_draw}),
    .Out_Clear({dreg_58_out_clear, dreg_59_out_clear}), .Button({undriven_59, undriven_60}),
    .Input_Overwrite(demultiplexer_2_out26), .Input(dreg_58_out_input),
    .Overwrite({undriven_122, undriven_123}), .Out_Input(dreg_59_out_input), .Output(Out_59),
    .overCMD(decoder_4_out26));
  dReg dreg_60 (
    .Enabled(decoder_2_out27), .Out_Draw({dreg_59_out_draw, dreg_60_out_draw}),
    .Out_Clear({dreg_59_out_clear, dreg_60_out_clear}), .Button({undriven_60, undriven_61}),
    .Input_Overwrite(demultiplexer_2_out27), .Input(dreg_59_out_input),
    .Overwrite({undriven_123, undriven_124}), .Out_Input(dreg_60_out_input), .Output(Out_60),
    .overCMD(decoder_4_out27));
  dReg dreg_61 (
    .Enabled(decoder_2_out28), .Out_Draw({dreg_60_out_draw, dreg_61_out_draw}),
    .Out_Clear({dreg_60_out_clear, dreg_61_out_clear}), .Button({undriven_61, undriven_62}),
    .Input_Overwrite(demultiplexer_2_out28), .Input(dreg_60_out_input),
    .Overwrite({undriven_124, undriven_125}), .Out_Input(dreg_61_out_input), .Output(Out_61),
    .overCMD(decoder_4_out28));
  dReg dreg_62 (
    .Enabled(decoder_2_out29), .Out_Draw({dreg_61_out_draw, dreg_62_out_draw}),
    .Out_Clear({dreg_61_out_clear, dreg_62_out_clear}), .Button({undriven_62, undriven_63}),
    .Input_Overwrite(demultiplexer_2_out29), .Input(dreg_61_out_input),
    .Overwrite({undriven_125, undriven_126}), .Out_Input(dreg_62_out_input), .Output(Out_62),
    .overCMD(decoder_4_out29));
  dReg dreg_63 (
    .Enabled(decoder_2_out30), .Out_Draw({dreg_62_out_draw, dreg_63_out_draw}),
    .Out_Clear({dreg_62_out_clear, dreg_63_out_clear}), .Button({undriven_63, undriven_64}),
    .Input_Overwrite(demultiplexer_2_out30), .Input(dreg_62_out_input),
    .Overwrite({undriven_126, undriven_127}), .Out_Input(dreg_63_out_input), .Output(Out_63),
    .overCMD(decoder_4_out30));
  dReg dreg_64 (
    .Enabled(decoder_2_out31), .Out_Draw({dreg_63_out_draw, dreg_64_out_draw}),
    .Out_Clear({dreg_63_out_clear, dreg_64_out_clear}), .Button({undriven_64, undriven}),
    .Input_Overwrite(demultiplexer_2_out31), .Input(dreg_63_out_input),
    .Overwrite({undriven_127, undriven_128}), .Out_Input(dreg_64_out_input), .Output(Out_64),
    .overCMD(decoder_4_out31));
  // Probe on dreg_64_out_draw
  // Probe on dreg_64_out_input
  and and_1 (and_1_out, C, ~Loading);  // AND_Gate
  // Probe on undriven
  // Probe on dreg_64_out_clear
  // Probe on undriven_128
  Demultiplexer #(.select(5), .width(32)) demultiplexer_1 (
    .out0(demultiplexer_1_out0), .out1(demultiplexer_1_out1), .out2(demultiplexer_1_out2),
    .out3(demultiplexer_1_out3), .out4(demultiplexer_1_out4), .out5(demultiplexer_1_out5),
    .out6(demultiplexer_1_out6), .out7(demultiplexer_1_out7), .out8(demultiplexer_1_out8),
    .out9(demultiplexer_1_out9), .out10(demultiplexer_1_out10), .out11(demultiplexer_1_out11),
    .out12(demultiplexer_1_out12), .out13(demultiplexer_1_out13), .out14(demultiplexer_1_out14),
    .out15(demultiplexer_1_out15), .out16(demultiplexer_1_out16), .out17(demultiplexer_1_out17),
    .out18(demultiplexer_1_out18), .out19(demultiplexer_1_out19), .out20(demultiplexer_1_out20),
    .out21(demultiplexer_1_out21), .out22(demultiplexer_1_out22), .out23(demultiplexer_1_out23),
    .out24(demultiplexer_1_out24), .out25(demultiplexer_1_out25), .out26(demultiplexer_1_out26),
    .out27(demultiplexer_1_out27), .out28(demultiplexer_1_out28), .out29(demultiplexer_1_out29),
    .out30(demultiplexer_1_out30), .out31(demultiplexer_1_out31), .in(CD1), .sel(CA), .en(undriven_96));
  Decoder #(.select(5)) decoder_3 (
    .out0(decoder_3_out0), .out1(decoder_3_out1), .out2(decoder_3_out2), .out3(decoder_3_out3),
    .out4(decoder_3_out4), .out5(decoder_3_out5), .out6(decoder_3_out6), .out7(decoder_3_out7),
    .out8(decoder_3_out8), .out9(decoder_3_out9), .out10(decoder_3_out10), .out11(decoder_3_out11),
    .out12(decoder_3_out12), .out13(decoder_3_out13), .out14(decoder_3_out14), .out15(decoder_3_out15),
    .out16(decoder_3_out16), .out17(decoder_3_out17), .out18(decoder_3_out18), .out19(decoder_3_out19),
    .out20(decoder_3_out20), .out21(decoder_3_out21), .out22(decoder_3_out22), .out23(decoder_3_out23),
    .out24(decoder_3_out24), .out25(decoder_3_out25), .out26(decoder_3_out26), .out27(decoder_3_out27),
    .out28(decoder_3_out28), .out29(decoder_3_out29), .out30(decoder_3_out30), .out31(decoder_3_out31),
    .sel(CA), .en(undriven_96));
  Decoder #(.select(5)) decoder_4 (
    .out0(decoder_4_out0), .out1(decoder_4_out1), .out2(decoder_4_out2), .out3(decoder_4_out3),
    .out4(decoder_4_out4), .out5(decoder_4_out5), .out6(decoder_4_out6), .out7(decoder_4_out7),
    .out8(decoder_4_out8), .out9(decoder_4_out9), .out10(decoder_4_out10), .out11(decoder_4_out11),
    .out12(decoder_4_out12), .out13(decoder_4_out13), .out14(decoder_4_out14), .out15(decoder_4_out15),
    .out16(decoder_4_out16), .out17(decoder_4_out17), .out18(decoder_4_out18), .out19(decoder_4_out19),
    .out20(decoder_4_out20), .out21(decoder_4_out21), .out22(decoder_4_out22), .out23(decoder_4_out23),
    .out24(decoder_4_out24), .out25(decoder_4_out25), .out26(decoder_4_out26), .out27(decoder_4_out27),
    .out28(decoder_4_out28), .out29(decoder_4_out29), .out30(decoder_4_out30), .out31(decoder_4_out31),
    .sel(CA), .en(undriven_96));
  Demultiplexer #(.select(5), .width(32)) demultiplexer_2 (
    .out0(demultiplexer_2_out0), .out1(demultiplexer_2_out1), .out2(demultiplexer_2_out2),
    .out3(demultiplexer_2_out3), .out4(demultiplexer_2_out4), .out5(demultiplexer_2_out5),
    .out6(demultiplexer_2_out6), .out7(demultiplexer_2_out7), .out8(demultiplexer_2_out8),
    .out9(demultiplexer_2_out9), .out10(demultiplexer_2_out10), .out11(demultiplexer_2_out11),
    .out12(demultiplexer_2_out12), .out13(demultiplexer_2_out13), .out14(demultiplexer_2_out14),
    .out15(demultiplexer_2_out15), .out16(demultiplexer_2_out16), .out17(demultiplexer_2_out17),
    .out18(demultiplexer_2_out18), .out19(demultiplexer_2_out19), .out20(demultiplexer_2_out20),
    .out21(demultiplexer_2_out21), .out22(demultiplexer_2_out22), .out23(demultiplexer_2_out23),
    .out24(demultiplexer_2_out24), .out25(demultiplexer_2_out25), .out26(demultiplexer_2_out26),
    .out27(demultiplexer_2_out27), .out28(demultiplexer_2_out28), .out29(demultiplexer_2_out29),
    .out30(demultiplexer_2_out30), .out31(demultiplexer_2_out31), .in(CD2), .sel(CA), .en(undriven_96));
  Button button_1 ();  // open: out
  or or_1 (or_1_out, Loading, Saving);
  and and_2 (and_2_out, counter_1_carry, Saving);
  and and_3 (and_3_out, ~or_1_out, Save);  // AND_Gate
  or or_2 (or_2_out, and_3_out, and_2_out);
  T_Flip_Flop t_ff_1 (.clk(or_2_out), .T(or_2_out), .Q(Saving));  // open: Qn, preset, reset, en
  Button button_2 ();  // open: out
  or or_3 (or_3_out, Loading, Saving);
  and and_4 (and_4_out, counter_1_carry, Loading);
  and and_5 (and_5_out, ~or_3_out, Load);  // AND_Gate
  or or_4 (or_4_out, and_5_out, and_4_out);
  T_Flip_Flop t_ff_2 (.clk(or_4_out), .T(or_4_out), .Q(Loading));  // open: Qn, preset, reset, en
  Clock clock_1 (.out(clock_1_out));
  or or_5 (or_5_out, Saving, Loading);
  and and_6 (and_6_out, or_5_out, ~counter_1_carry);  // AND_Gate
  or or_6 (or_6_out, Saving, Loading, and_6_out);
  assign Cl = or_6_out ? clock_1_out : 1'bz;  // Controlled_Buffer controlled_buffer_3
  Counter #(.width(5), .max('h1f), .ongoal("stay")) counter_1 (
    .count(Cl), .Q(CA), .carry(counter_1_carry), .clk(Cl), .clr(counter_1_carry));  // open: load, D
  Multiplexer #(.select(5), .width(32)) multiplexer_1 (
    .in0(Out_1), .in1(Out_2), .in2(Out_3), .in3(Out_4), .in4(Out_5), .in5(Out_6), .in6(Out_7), .in7(Out_8),
    .in8(Out_9), .in9(Out_10), .in10(Out_11), .in11(Out_12), .in12(Out_13), .in13(Out_14), .in14(Out_15),
    .in15(Out_16), .in16(Out_17), .in17(Out_18), .in18(Out_19), .in19(Out_20), .in20(Out_21), .in21(Out_22),
    .in22(Out_23), .in23(Out_24), .in24(Out_25), .in25(Out_26), .in26(Out_27), .in27(Out_28), .in28(Out_29),
    .in29(Out_30), .in30(Out_31), .in31(Out_32), .out(multiplexer_1_out), .sel(CA), .en(Saving));
  Multiplexer #(.select(5), .width(32)) multiplexer_2 (
    .in0(Out_33), .in1(Out_34), .in2(Out_35), .in3(Out_36), .in4(Out_37), .in5(Out_38), .in6(Out_39),
    .in7(Out_40), .in8(Out_41), .in9(Out_42), .in10(Out_43), .in11(Out_44), .in12(Out_45), .in13(Out_46),
    .in14(Out_47), .in15(Out_48), .in16(Out_49), .in17(Out_50), .in18(Out_51), .in19(Out_52), .in20(Out_53),
    .in21(Out_54), .in22(Out_55), .in23(Out_56), .in24(Out_57), .in25(Out_58), .in26(Out_59), .in27(Out_60),
    .in28(Out_61), .in29(Out_62), .in30(Out_63), .in31(Out_64), .out(multiplexer_2_out), .sel(CA), .en(Saving));
  RAM #(.addrWidth(5), .dataWidth(32), .bus("separate")) ram_1 (
    .din(multiplexer_1_out), .data(CD1), .str(Saving), .clk(Cl), .ld(Loading), .clr(Erase_memory));  // open: addr, sel
  RAM #(.addrWidth(5), .dataWidth(32), .bus("separate")) ram_2 (
    .addr(CA), .din(multiplexer_2_out), .data(CD2), .str(Saving), .clk(Cl), .ld(Loading), .clr(Erase_memory));  // open: sel

  // Other names for the same wires on the sheet: D = Draw; E = Erase_memory; L = Load; Ling = Loading; M = Move;
  //   R = Reset; S = Save; Sing = Saving

  // Notes on the sheet:
  //   Old reg array
endmodule

module nReg (
  input  Enabled,
  input  Clear,
  input  Button,
  input  [31:0] Input,
  output [31:0] Output,
  output Out_Clear,
  output Out_Button,
  output [31:0] Out_Input
);

  wire bitselector_1_out, controlled_buffer_1_out, not_1_out;
  wire [4:0] bitfinder_1_index;
  wire [31:0] adder_1_out, controlled_buffer_2_out, controlled_buffer_3_out, controlled_buffer_4_out;

  Register #(.width(32)) register_1 (
    .D(adder_1_out), .Q(Output), .clk(controlled_buffer_1_out), .clr(Clear));  // open: en
  assign controlled_buffer_1_out = Enabled ? Button : 1'bz;  // Controlled_Buffer controlled_buffer_1
  assign controlled_buffer_2_out = not_1_out ? Output : 32'bz;  // Controlled_Buffer controlled_buffer_2
  not not_1 (not_1_out, bitselector_1_out);
  BitSelector #(.width(32)) bitselector_1 (.in(Output), .out(bitselector_1_out), .sel(bitfinder_1_index));
  assign controlled_buffer_3_out = not_1_out ? controlled_buffer_4_out : 32'bz;  // Controlled_Buffer controlled_buffer_3
  assign controlled_buffer_4_out = Enabled ? Input : 32'bz;  // Controlled_Buffer controlled_buffer_4
  BitFinder #(.width(32)) bitfinder_1 (.in(controlled_buffer_4_out), .index(bitfinder_1_index));  // open: found
  Adder #(.width(32)) adder_1 (
    .a(controlled_buffer_2_out), .b(controlled_buffer_3_out), .out(adder_1_out));  // open: cin, cout
  assign Out_Input = Input;  // Buffer buffer_1, 32 bits wide

  assign Out_Button = Button;
  assign Out_Clear = Clear;
endmodule

module cReg (
  input  Enabled,
  input  Draw_Mode,
  input  Clear,
  input  Button,
  input  [31:0] Input_Overwrite,
  input  [31:0] Input,
  input  Overwrite,
  output Out_Draw,
  output Out_Clear,
  output Out_Button,
  output [31:0] Out_Input,
  output [31:0] Output,
  output Out_Overwrite
);

  wire not_1_out, not_2_out, not_3_out, not_4_out, not_5_out, not_6_out, not_7_out, not_8_out, not_9_out,
       not_10_out, not_11_out, not_12_out, not_13_out, not_14_out, not_15_out, not_16_out, not_17_out,
       not_18_out, not_19_out, not_20_out, not_21_out, not_22_out, not_23_out, not_24_out, not_25_out,
       not_26_out, not_27_out, not_28_out, not_29_out, not_30_out, not_31_out, not_32_out, not_33_out,
       not_34_out, or_33_out;
  wire [31:0] and_1_out, controlled_buffer_1_out, controlled_buffer_2_out, controlled_buffer_3_out,
       controlled_buffer_4_out, or_1_out;

  assign controlled_buffer_1_out = Enabled ? Input : 32'bz;  // Controlled_Buffer controlled_buffer_1
  or or_1 (or_1_out[0], controlled_buffer_2_out[0], Output[0]);
  or or_2 (or_1_out[1], controlled_buffer_2_out[1], Output[1]);
  or or_3 (or_1_out[2], controlled_buffer_2_out[2], Output[2]);
  or or_4 (or_1_out[3], controlled_buffer_2_out[3], Output[3]);
  or or_5 (or_1_out[4], controlled_buffer_2_out[4], Output[4]);
  or or_6 (or_1_out[5], controlled_buffer_2_out[5], Output[5]);
  or or_7 (or_1_out[6], controlled_buffer_2_out[6], Output[6]);
  or or_8 (or_1_out[7], controlled_buffer_2_out[7], Output[7]);
  or or_9 (or_1_out[8], controlled_buffer_2_out[8], Output[8]);
  or or_10 (or_1_out[9], controlled_buffer_2_out[9], Output[9]);
  or or_11 (or_1_out[10], controlled_buffer_2_out[10], Output[10]);
  or or_12 (or_1_out[11], controlled_buffer_2_out[11], Output[11]);
  or or_13 (or_1_out[12], controlled_buffer_2_out[12], Output[12]);
  or or_14 (or_1_out[13], controlled_buffer_2_out[13], Output[13]);
  or or_15 (or_1_out[14], controlled_buffer_2_out[14], Output[14]);
  or or_16 (or_1_out[15], controlled_buffer_2_out[15], Output[15]);
  or or_17 (or_1_out[16], controlled_buffer_2_out[16], Output[16]);
  or or_18 (or_1_out[17], controlled_buffer_2_out[17], Output[17]);
  or or_19 (or_1_out[18], controlled_buffer_2_out[18], Output[18]);
  or or_20 (or_1_out[19], controlled_buffer_2_out[19], Output[19]);
  or or_21 (or_1_out[20], controlled_buffer_2_out[20], Output[20]);
  or or_22 (or_1_out[21], controlled_buffer_2_out[21], Output[21]);
  or or_23 (or_1_out[22], controlled_buffer_2_out[22], Output[22]);
  or or_24 (or_1_out[23], controlled_buffer_2_out[23], Output[23]);
  or or_25 (or_1_out[24], controlled_buffer_2_out[24], Output[24]);
  or or_26 (or_1_out[25], controlled_buffer_2_out[25], Output[25]);
  or or_27 (or_1_out[26], controlled_buffer_2_out[26], Output[26]);
  or or_28 (or_1_out[27], controlled_buffer_2_out[27], Output[27]);
  or or_29 (or_1_out[28], controlled_buffer_2_out[28], Output[28]);
  or or_30 (or_1_out[29], controlled_buffer_2_out[29], Output[29]);
  or or_31 (or_1_out[30], controlled_buffer_2_out[30], Output[30]);
  or or_32 (or_1_out[31], controlled_buffer_2_out[31], Output[31]);
  assign controlled_buffer_2_out = Draw_Mode ? controlled_buffer_1_out : 32'bz;  // Controlled_Buffer controlled_buffer_2
  assign controlled_buffer_3_out = not_2_out ? controlled_buffer_1_out : 32'bz;  // Controlled_Buffer controlled_buffer_3
  not not_1 (not_1_out, controlled_buffer_3_out[0]);
  not not_2 (not_2_out, Draw_Mode);
  not not_3 (not_3_out, controlled_buffer_3_out[1]);
  not not_4 (not_4_out, controlled_buffer_3_out[2]);
  and and_1 (and_1_out[0], not_1_out, Output[0]);
  not not_5 (not_5_out, controlled_buffer_3_out[3]);
  not not_6 (not_6_out, controlled_buffer_3_out[4]);
  and and_2 (and_1_out[1], not_3_out, Output[1]);
  and and_3 (and_1_out[2], not_4_out, Output[2]);
  not not_7 (not_7_out, controlled_buffer_3_out[5]);
  not not_8 (not_8_out, controlled_buffer_3_out[6]);
  and and_4 (and_1_out[3], not_5_out, Output[3]);
  not not_9 (not_9_out, controlled_buffer_3_out[7]);
  and and_5 (and_1_out[4], not_6_out, Output[4]);
  not not_10 (not_10_out, controlled_buffer_3_out[8]);
  and and_6 (and_1_out[5], not_7_out, Output[5]);
  not not_11 (not_11_out, controlled_buffer_3_out[9]);
  and and_7 (and_1_out[6], not_8_out, Output[6]);
  and and_8 (and_1_out[7], not_9_out, Output[7]);
  not not_12 (not_12_out, controlled_buffer_3_out[10]);
  not not_13 (not_13_out, controlled_buffer_3_out[11]);
  and and_9 (and_1_out[8], not_10_out, Output[8]);
  not not_14 (not_14_out, controlled_buffer_3_out[12]);
  and and_10 (and_1_out[9], not_11_out, Output[9]);
  not not_15 (not_15_out, controlled_buffer_3_out[13]);
  and and_11 (and_1_out[10], not_12_out, Output[10]);
  and and_12 (and_1_out[11], not_13_out, Output[11]);
  not not_16 (not_16_out, controlled_buffer_3_out[14]);
  and and_13 (and_1_out[12], not_14_out, Output[12]);
  not not_17 (not_17_out, controlled_buffer_3_out[15]);
  not not_18 (not_18_out, controlled_buffer_3_out[16]);
  and and_14 (and_1_out[13], not_15_out, Output[13]);
  not not_19 (not_19_out, controlled_buffer_3_out[17]);
  and and_15 (and_1_out[14], not_16_out, Output[14]);
  and and_16 (and_1_out[15], not_17_out, Output[15]);
  not not_20 (not_20_out, controlled_buffer_3_out[18]);
  and and_17 (and_1_out[16], not_18_out, Output[16]);
  not not_21 (not_21_out, controlled_buffer_3_out[19]);
  not not_22 (not_22_out, controlled_buffer_3_out[20]);
  and and_18 (and_1_out[17], not_19_out, Output[17]);
  not not_23 (not_23_out, controlled_buffer_3_out[21]);
  and and_19 (and_1_out[18], not_20_out, Output[18]);
  not not_24 (not_24_out, controlled_buffer_3_out[22]);
  and and_20 (and_1_out[19], not_21_out, Output[19]);
  and and_21 (and_1_out[20], not_22_out, Output[20]);
  not not_25 (not_25_out, controlled_buffer_3_out[23]);
  not not_26 (not_26_out, controlled_buffer_3_out[24]);
  and and_22 (and_1_out[21], not_23_out, Output[21]);
  and and_23 (and_1_out[22], not_24_out, Output[22]);
  not not_27 (not_27_out, controlled_buffer_3_out[25]);
  and and_24 (and_1_out[23], not_25_out, Output[23]);
  not not_28 (not_28_out, controlled_buffer_3_out[26]);
  and and_25 (and_1_out[24], not_26_out, Output[24]);
  not not_29 (not_29_out, controlled_buffer_3_out[27]);
  and and_26 (and_1_out[25], not_27_out, Output[25]);
  not not_30 (not_30_out, controlled_buffer_3_out[28]);
  and and_27 (and_1_out[26], not_28_out, Output[26]);
  not not_31 (not_31_out, controlled_buffer_3_out[29]);
  and and_28 (and_1_out[27], not_29_out, Output[27]);
  not not_32 (not_32_out, controlled_buffer_3_out[30]);
  not not_33 (not_33_out, controlled_buffer_3_out[31]);
  and and_29 (and_1_out[28], not_30_out, Output[28]);
  and and_30 (and_1_out[29], not_31_out, Output[29]);
  and and_31 (and_1_out[30], not_32_out, Output[30]);
  and and_32 (and_1_out[31], not_33_out, Output[31]);
  // Probe on and_1_out
  not not_34 (not_34_out, Draw_Mode);
  assign controlled_buffer_4_out = Overwrite ? Input_Overwrite : 32'bz;  // Controlled_Buffer controlled_buffer_4
  assign controlled_buffer_4_out = Draw_Mode ? or_1_out : 32'bz;  // Controlled_Buffer controlled_buffer_5
  assign controlled_buffer_4_out = not_34_out ? and_1_out : 32'bz;  // Controlled_Buffer controlled_buffer_6
  Register #(.width(32)) register_1 (
    .D(controlled_buffer_4_out), .Q(Output), .clk(or_33_out), .clr(Clear));  // open: en
  or or_33 (or_33_out, Button, Overwrite);

  assign Out_Button = Button;
  assign Out_Clear = Clear;
  assign Out_Draw = Draw_Mode;
  assign Out_Input = Input;
  assign Out_Overwrite = Overwrite;

  // Other names for the same wires on the sheet: btn = Button; clr = Clear; drw = Draw_Mode; ena = Enabled;
  //   ovr = Overwrite
endmodule

module dReg (
  input  Enabled,
  input  Draw_Mode,
  input  [31:0] Input_Overwrite,
  input  Clear,
  input  Button,
  input  [31:0] Input,
  input  Overwrite,
  input  overCMD,
  output Out_Draw,
  output Out_Clear,
  output Out_Button,
  output [31:0] Out_Input,
  output [31:0] Output,
  output Out_Overwrite
);

  wire and_33_out, and_34_out, ena, not_1_out, not_2_out, not_3_out, not_4_out, not_5_out, not_6_out,
       not_7_out, not_8_out, not_9_out, not_10_out, not_11_out, not_12_out, not_13_out, not_14_out,
       not_15_out, not_16_out, not_17_out, not_18_out, not_19_out, not_20_out, not_21_out, not_22_out,
       not_23_out, not_24_out, not_25_out, not_26_out, not_27_out, not_28_out, not_29_out, not_30_out,
       not_31_out, not_32_out, not_33_out, or_34_out;
  wire [31:0] and_1_out, controlled_buffer_1_out, controlled_buffer_2_out, controlled_buffer_3_out,
       controlled_buffer_4_out, or_2_out;

  or or_1 (ena, Enabled, Overwrite);
  assign controlled_buffer_1_out = ena ? Input : 32'bz;  // Controlled_Buffer controlled_buffer_1
  assign controlled_buffer_2_out = Draw_Mode ? controlled_buffer_1_out : 32'bz;  // Controlled_Buffer controlled_buffer_2
  assign controlled_buffer_3_out = not_1_out ? controlled_buffer_1_out : 32'bz;  // Controlled_Buffer controlled_buffer_3
  not not_1 (not_1_out, Draw_Mode);
  or or_2 (or_2_out[0], controlled_buffer_2_out[0], Output[0]);
  or or_3 (or_2_out[1], controlled_buffer_2_out[1], Output[1]);
  or or_4 (or_2_out[2], controlled_buffer_2_out[2], Output[2]);
  or or_5 (or_2_out[3], controlled_buffer_2_out[3], Output[3]);
  or or_6 (or_2_out[4], controlled_buffer_2_out[4], Output[4]);
  or or_7 (or_2_out[5], controlled_buffer_2_out[5], Output[5]);
  or or_8 (or_2_out[6], controlled_buffer_2_out[6], Output[6]);
  or or_9 (or_2_out[7], controlled_buffer_2_out[7], Output[7]);
  or or_10 (or_2_out[8], controlled_buffer_2_out[8], Output[8]);
  or or_11 (or_2_out[9], controlled_buffer_2_out[9], Output[9]);
  or or_12 (or_2_out[10], controlled_buffer_2_out[10], Output[10]);
  or or_13 (or_2_out[11], controlled_buffer_2_out[11], Output[11]);
  or or_14 (or_2_out[12], controlled_buffer_2_out[12], Output[12]);
  or or_15 (or_2_out[13], controlled_buffer_2_out[13], Output[13]);
  or or_16 (or_2_out[14], controlled_buffer_2_out[14], Output[14]);
  or or_17 (or_2_out[15], controlled_buffer_2_out[15], Output[15]);
  or or_18 (or_2_out[16], controlled_buffer_2_out[16], Output[16]);
  or or_19 (or_2_out[17], controlled_buffer_2_out[17], Output[17]);
  or or_20 (or_2_out[18], controlled_buffer_2_out[18], Output[18]);
  or or_21 (or_2_out[19], controlled_buffer_2_out[19], Output[19]);
  or or_22 (or_2_out[20], controlled_buffer_2_out[20], Output[20]);
  or or_23 (or_2_out[21], controlled_buffer_2_out[21], Output[21]);
  or or_24 (or_2_out[22], controlled_buffer_2_out[22], Output[22]);
  or or_25 (or_2_out[23], controlled_buffer_2_out[23], Output[23]);
  or or_26 (or_2_out[24], controlled_buffer_2_out[24], Output[24]);
  or or_27 (or_2_out[25], controlled_buffer_2_out[25], Output[25]);
  or or_28 (or_2_out[26], controlled_buffer_2_out[26], Output[26]);
  or or_29 (or_2_out[27], controlled_buffer_2_out[27], Output[27]);
  or or_30 (or_2_out[28], controlled_buffer_2_out[28], Output[28]);
  or or_31 (or_2_out[29], controlled_buffer_2_out[29], Output[29]);
  or or_32 (or_2_out[30], controlled_buffer_2_out[30], Output[30]);
  or or_33 (or_2_out[31], controlled_buffer_2_out[31], Output[31]);
  not not_2 (not_2_out, controlled_buffer_3_out[0]);
  not not_3 (not_3_out, controlled_buffer_3_out[1]);
  not not_4 (not_4_out, controlled_buffer_3_out[2]);
  and and_1 (and_1_out[0], not_2_out, Output[0]);
  not not_5 (not_5_out, controlled_buffer_3_out[3]);
  and and_2 (and_1_out[1], not_3_out, Output[1]);
  not not_6 (not_6_out, controlled_buffer_3_out[4]);
  and and_3 (and_1_out[2], not_4_out, Output[2]);
  not not_7 (not_7_out, controlled_buffer_3_out[5]);
  and and_4 (and_1_out[3], not_5_out, Output[3]);
  not not_8 (not_8_out, controlled_buffer_3_out[6]);
  and and_5 (and_1_out[4], not_6_out, Output[4]);
  not not_9 (not_9_out, controlled_buffer_3_out[7]);
  and and_6 (and_1_out[5], not_7_out, Output[5]);
  not not_10 (not_10_out, controlled_buffer_3_out[8]);
  not not_11 (not_11_out, controlled_buffer_3_out[9]);
  and and_7 (and_1_out[6], not_8_out, Output[6]);
  not not_12 (not_12_out, controlled_buffer_3_out[10]);
  and and_8 (and_1_out[7], not_9_out, Output[7]);
  not not_13 (not_13_out, controlled_buffer_3_out[11]);
  and and_9 (and_1_out[8], not_10_out, Output[8]);
  not not_14 (not_14_out, controlled_buffer_3_out[12]);
  and and_10 (and_1_out[9], not_11_out, Output[9]);
  not not_15 (not_15_out, controlled_buffer_3_out[13]);
  and and_11 (and_1_out[10], not_12_out, Output[10]);
  and and_12 (and_1_out[11], not_13_out, Output[11]);
  not not_16 (not_16_out, controlled_buffer_3_out[14]);
  not not_17 (not_17_out, controlled_buffer_3_out[15]);
  and and_13 (and_1_out[12], not_14_out, Output[12]);
  and and_14 (and_1_out[13], not_15_out, Output[13]);
  not not_18 (not_18_out, controlled_buffer_3_out[16]);
  not not_19 (not_19_out, controlled_buffer_3_out[17]);
  and and_15 (and_1_out[14], not_16_out, Output[14]);
  not not_20 (not_20_out, controlled_buffer_3_out[18]);
  and and_16 (and_1_out[15], not_17_out, Output[15]);
  not not_21 (not_21_out, controlled_buffer_3_out[19]);
  and and_17 (and_1_out[16], not_18_out, Output[16]);
  not not_22 (not_22_out, controlled_buffer_3_out[20]);
  and and_18 (and_1_out[17], not_19_out, Output[17]);
  not not_23 (not_23_out, controlled_buffer_3_out[21]);
  and and_19 (and_1_out[18], not_20_out, Output[18]);
  and and_20 (and_1_out[19], not_21_out, Output[19]);
  not not_24 (not_24_out, controlled_buffer_3_out[22]);
  not not_25 (not_25_out, controlled_buffer_3_out[23]);
  and and_21 (and_1_out[20], not_22_out, Output[20]);
  not not_26 (not_26_out, controlled_buffer_3_out[24]);
  and and_22 (and_1_out[21], not_23_out, Output[21]);
  not not_27 (not_27_out, controlled_buffer_3_out[25]);
  and and_23 (and_1_out[22], not_24_out, Output[22]);
  and and_24 (and_1_out[23], not_25_out, Output[23]);
  not not_28 (not_28_out, controlled_buffer_3_out[26]);
  and and_25 (and_1_out[24], not_26_out, Output[24]);
  not not_29 (not_29_out, controlled_buffer_3_out[27]);
  not not_30 (not_30_out, controlled_buffer_3_out[28]);
  and and_26 (and_1_out[25], not_27_out, Output[25]);
  and and_27 (and_1_out[26], not_28_out, Output[26]);
  not not_31 (not_31_out, controlled_buffer_3_out[29]);
  not not_32 (not_32_out, controlled_buffer_3_out[30]);
  and and_28 (and_1_out[27], not_29_out, Output[27]);
  and and_29 (and_1_out[28], not_30_out, Output[28]);
  not not_33 (not_33_out, controlled_buffer_3_out[31]);
  and and_30 (and_1_out[29], not_31_out, Output[29]);
  and and_31 (and_1_out[30], not_32_out, Output[30]);
  and and_32 (and_1_out[31], not_33_out, Output[31]);
  // Probe on and_1_out
  and and_33 (and_33_out, Draw_Mode, ~Overwrite);  // AND_Gate
  assign controlled_buffer_4_out = and_33_out ? or_2_out : 32'bz;  // Controlled_Buffer controlled_buffer_4
  assign controlled_buffer_4_out = and_34_out ? and_1_out : 32'bz;  // Controlled_Buffer controlled_buffer_5
  and and_34 (and_34_out, ~Draw_Mode, ~Overwrite);  // AND_Gate
  assign controlled_buffer_4_out = Overwrite ? Input_Overwrite : 32'bz;  // Controlled_Buffer controlled_buffer_6
  Register #(.width(32), .trigger("high")) register_1 (
    .D(controlled_buffer_4_out), .Q(Output), .clk(or_34_out), .clr(Clear));  // open: en
  or or_34 (or_34_out, Button, overCMD);

  assign Out_Button = Button;
  assign Out_Clear = Clear;
  assign Out_Draw = Draw_Mode;
  assign Out_Input = Input;
  assign Out_Overwrite = Overwrite;

  // Other names for the same wires on the sheet: btn = Button; clr = Clear; drw = Draw_Mode; ovr = Overwrite
endmodule
